// Logisim project cpu21-riscv.circ as structural Verilog: 16 circuits, main circuit ◇单周期RISC-V
module \单周期RISC_V  (
  input  IR1,
  input  IR2,
  input  IR3,
  output RegWrite,
  output MemWrite,
  output [31:0] PC,
  output [31:0] IR,
  output [31:0] RDin,
  output [31:0] MDin,
  output [31:0] LedData
);

  wire and_2_out, and_4_out, CLK, clock_2_out, comparator_1_eq, comparator_2_eq, comparator_3_eq,
       comparator_3_lt, d_ff_1_q, ecall, Go, halt, IR1_t, IR2_t, IR3_t, IRA, IRB, IRC, LB, LUI, MemToReg,
       nand_1_out, not_1_out, not_2_out, not_3_out, PC_4__Reg, ResEQ, ResLT, RST, SType, W1, W2, W3,
       \单周期硬布线控制器_1_alu_src , \单周期硬布线控制器_1_beq , \单周期硬布线控制器_1_bltu , \单周期硬布线控制器_1_bne , \单周期硬布线控制器_1_jal ,
       \单周期硬布线控制器_1_jalr ;
  wire [2:0] priority_encoder_1_out;
  wire [3:0] \单周期硬布线控制器_1_alu_op ;
  wire [4:0] multiplexer_6_out, multiplexer_7_out;
  wire [7:0] multiplexer_13_out;
  wire [11:0] multiplexer_5_out;
  wire [12:0] CNT_num;
  wire [15:0] \总周期数 ;
  wire [31:0] alu_1_result, and_1_out, bit_extender_2_out, bit_extender_3_out, bit_extender_4_out, BXXpc,
       imm12ext, JALpc, jalrPC, multiplexer_1_out, multiplexer_2_out, multiplexer_3_out, multiplexer_4_out,
       multiplexer_9_out, multiplexer_10_out, multiplexer_11_out, multiplexer_12_out, PC_4, ram_1_data,
       RegR1, shifter_1_out, shifter_2_out;

  Clock #(.highDuration(1), .lowDuration(1)) clock_1 ();  // open: out
  Button _1 (.out(IRA));
  Button _2 (.out(IRB));
  Button _3 (.out(IRC));
  Button \u_继续运行  (.out(Go));
  LED #(.active("true")) led_1 (.in(W1));
  LED #(.active("true")) led_2 (.in(W2));
  LED #(.active("true")) led_3 (.in(W3));
  Hex_Digit_Display hex_digit_display_1 (.value(LedData[31:28]));  // open: dp
  Multiplexer #(.select(1), .width(32), .disabled("Z"), .enable("false")) multiplexer_1 (
    .in0(PC_4), .in1(BXXpc), .out(multiplexer_1_out), .sel(ResEQ));
  Multiplexer #(.select(1), .width(32), .disabled("Z"), .enable("false")) multiplexer_2 (
    .in0(BXXpc), .in1(PC_4), .out(multiplexer_2_out), .sel(ResEQ));
  Multiplexer #(.select(1), .width(32), .disabled("Z"), .enable("false")) multiplexer_3 (
    .in0(PC_4), .in1(BXXpc), .out(multiplexer_3_out), .sel(ResLT));
  Hex_Digit_Display hex_digit_display_2 (.value(LedData[23:20]));  // open: dp
  Hex_Digit_Display hex_digit_display_3 (.value(LedData[27:24]));  // open: dp
  Multiplexer #(.select(3), .width(32), .disabled("Z"), .enable("false")) multiplexer_4 (
    .in0(PC_4), .in1(jalrPC), .in2(JALpc), .in3(multiplexer_1_out), .in4(multiplexer_2_out),
    .in5(multiplexer_3_out), .out(multiplexer_4_out), .sel(priority_encoder_1_out));  // open: in6, in7
  Hex_Digit_Display hex_digit_display_4 (.value(LedData[15:12]));  // open: dp
  Hex_Digit_Display hex_digit_display_5 (.value(LedData[19:16]));  // open: dp
  Register #(.width(32), .trigger("rising"), .Select("low")) u_PC (
    .D(multiplexer_4_out), .en(not_1_out), .Q(PC), .clk(CLK), .clr(RST));
  not not_1 (not_1_out, halt);
  Hex_Digit_Display hex_digit_display_6 (.value(LedData[7:4]));  // open: dp
  Hex_Digit_Display hex_digit_display_7 (.value(LedData[11:8]));  // open: dp
  // Probe on \总周期数 
  Adder #(.width(32)) adder_1 (.a(PC), .b(32'h4), .out(PC_4));  // open: cin, cout
  Hex_Digit_Display hex_digit_display_8 (.value(LedData[3:0]));  // open: dp
  // RiscV_Probe riscv_probe_1: pin names not known; wires that end beside it: IR
  or or_1 (PC_4__Reg, \单周期硬布线控制器_1_jal , \单周期硬布线控制器_1_jalr );
  ROM #(.addrWidth(10), .dataWidth(32), .Select("high")) rom_1 (.addr(PC[11:2]), .data(IR));
  or or_2 (IR1_t, IR1, IRA);
  Priority_Encoder #(.select(3), .disabled(0)) priority_encoder_1 (
    .in0(1'b1), .in1(\单周期硬布线控制器_1_jalr ), .in2(\单周期硬布线控制器_1_jal ), .in3(\单周期硬布线控制器_1_beq ),
    .in4(\单周期硬布线控制器_1_bne ), .in5(\单周期硬布线控制器_1_bltu ), .out(priority_encoder_1_out), .en_in(1'b1));  // open: in6, in7, gs, en_out
  assign and_1_out = IR & 32'hfffff000;  // AND_Gate and_1, 32 bits wide
  or or_3 (IR2_t, IR2, IRB);
  \单周期硬布线控制器  \u_单周期硬布线控制器_1  (
    .Funct({IR[30], IR[25], IR[14:12]}), .OP(IR[6:2]), .ALU_OP(\单周期硬布线控制器_1_alu_op ), .MemToReg(MemToReg),
    .MemWrite(MemWrite), .ALU_SRC(\单周期硬布线控制器_1_alu_src ), .RegWrite(RegWrite), .ecall(ecall), .S_type(SType),
    .Jalr(\单周期硬布线控制器_1_jalr ), .Beq(\单周期硬布线控制器_1_beq ), .JAL(\单周期硬布线控制器_1_jal ), .Bne(\单周期硬布线控制器_1_bne ),
    .BLTU(\单周期硬布线控制器_1_bltu ), .LB(LB), .LUI(LUI));  // open: NotNop
  Multiplexer #(.select(1), .width(12), .disabled("Z"), .enable("false")) multiplexer_5 (
    .in0(IR[31:20]), .in1({IR[31:25], IR[11:7]}), .out(multiplexer_5_out), .sel(SType));
  assign imm12ext = {{20{multiplexer_5_out[11]}}, multiplexer_5_out};  // Bit_Extender bit_extender_1
  assign bit_extender_2_out = {{20{IR[31]}}, {IR[31], IR[7], IR[30:25], IR[11:8]}};  // Bit_Extender bit_extender_2
  assign bit_extender_3_out = {{12{IR[31]}}, {IR[31], IR[19:12], IR[20], IR[30:21]}};  // Bit_Extender bit_extender_3
  or or_4 (IR3_t, IR3, IRC);
  Multiplexer #(.select(1), .width(5), .disabled("Z"), .enable("false")) multiplexer_6 (
    .in0(IR[24:20]), .in1(5'b10001), .out(multiplexer_6_out), .sel(ecall));
  Shifter #(.width(32), .shift("ll")) shifter_1 (.in(bit_extender_2_out), .\dist (5'b00001), .out(shifter_1_out));
  Shifter #(.width(32), .shift("ll")) shifter_2 (.in(bit_extender_3_out), .\dist (5'b00001), .out(shifter_2_out));
  Multiplexer #(.select(1), .width(5), .disabled("Z"), .enable("false")) multiplexer_7 (
    .in0(IR[19:15]), .in1(5'b01010), .out(multiplexer_7_out), .sel(ecall));
  Adder #(.width(32)) adder_2 (.a(PC), .b(shifter_1_out), .out(BXXpc));  // open: cin, cout
  Adder #(.width(32)) adder_3 (.a(PC), .b(shifter_2_out), .out(JALpc));  // open: cin, cout
  and and_2 (and_2_out, ecall, comparator_1_eq);
  Comparator #(.width(32), .mode("twosComplement")) comparator_1 (
    .a(MDin), .b(32'h22), .eq(comparator_1_eq));  // open: gt, lt
  Multiplexer #(.select(1), .width(32), .disabled("Z"), .enable("false")) multiplexer_8 (
    .in0(multiplexer_9_out), .in1(PC_4), .out(RDin), .sel(PC_4__Reg));
  Regifile regifile_1 (
    .Din(RDin), .Clk(CLK), .R1(RegR1), .R2(MDin), .WE(RegWrite), .W_num(IR[11:7]),
    .R1_num(multiplexer_7_out), .R2_num(multiplexer_6_out));
  Register #(.width(32), .trigger("rising"), .Select("low")) register_1 (
    .D(RegR1), .en(and_2_out), .Q(LedData), .clk(CLK));  // open: clr
  Multiplexer #(.select(1), .width(32), .disabled("Z"), .enable("false")) multiplexer_9 (
    .in0(multiplexer_11_out), .in1(and_1_out), .out(multiplexer_9_out), .sel(LUI));
  Multiplexer #(.select(1), .width(32), .disabled("Z"), .enable("false")) multiplexer_10 (
    .in0(MDin), .in1(imm12ext), .out(multiplexer_10_out), .sel(\单周期硬布线控制器_1_alu_src ));
  Multiplexer #(.select(1), .width(32), .disabled("Z"), .enable("false")) multiplexer_11 (
    .in0(alu_1_result), .in1(multiplexer_12_out), .out(multiplexer_11_out), .sel(MemToReg));
  ALU alu_1 (
    .X(RegR1), .Y(multiplexer_10_out), .AluOP(\单周期硬布线控制器_1_alu_op ), .Equal(ResEQ), .Result(alu_1_result),
    .out_6(ResLT));  // open: Result_2, out_4
  D_Flip_Flop #(.trigger("high"), .Pre_Clr_Positions("LEGACY"), .NegatePresetClear("false"), .enable("true"), .NewFFLayout("false")) d_ff_1 (.Q(d_ff_1_q));  // open: clk, D, Qn, preset, en, reset
  // Probe on 13'h29b
  Comparator #(.width(32), .mode("twosComplement")) comparator_2 (
    .a(MDin), .b(32'ha), .eq(comparator_2_eq));  // open: gt, lt
  assign jalrPC = alu_1_result & 32'hfffffffe;  // AND_Gate and_3, 32 bits wide
  Multiplexer #(.select(1), .width(32), .disabled("Z"), .enable("false")) multiplexer_12 (
    .in0(ram_1_data), .in1(bit_extender_4_out), .out(multiplexer_12_out), .sel(LB));
  Comparator #(.width(13), .mode("twosComplement")) comparator_3 (
    .a(CNT_num), .b(13'h29b), .eq(comparator_3_eq), .lt(comparator_3_lt));  // open: gt
  Clock #(.highDuration(1), .lowDuration(1)) clock_2 (.out(clock_2_out));
  and and_4 (and_4_out, ecall, comparator_2_eq);
  Register #(.width(1), .trigger("falling"), .Select("low")) register_2 (
    .D(and_4_out), .en(not_2_out), .Q(halt), .clk(CLK), .clr(Go));
  not not_2 (not_2_out, halt);
  Counter #(.width(13), .max('h1fff), .ongoal("stay"), .trigger("rising"), .behavior("old")) counter_1 (
    .count(comparator_3_lt), .Q(CNT_num), .clk(clock_2_out));  // open: load, D, carry, clr, preset
  nand nand_1 (nand_1_out, d_ff_1_q, comparator_3_eq);
  not not_3 (not_3_out, halt);
  Counter #(.width(16), .max('hffff), .ongoal("stay"), .trigger("rising"), .behavior("new")) counter_2 (
    .count(not_3_out), .Q(\总周期数 ), .clk(CLK));  // open: load, D, carry, clr, preset, down
  assign CLK = nand_1_out ? clock_2_out : 1'bz;  // Controlled_Buffer controlled_buffer_1
  Pull_Resistor #(.pull(1)) pull_resistor_1 (.node(CLK));
  RAM #(.addrWidth(10), .dataWidth(32), .bus("separate"), .Select("high")) ram_1 (
    .addr(alu_1_result[11:2]), .din(MDin), .data(ram_1_data), .str(MemWrite), .clk(CLK));  // open: sel, ld, clr
  Multiplexer #(.select(2), .width(8), .disabled("Z"), .enable("false")) multiplexer_13 (
    .in0(ram_1_data[7:0]), .in1(ram_1_data[15:8]), .in2(ram_1_data[23:16]), .in3(ram_1_data[31:24]),
    .out(multiplexer_13_out), .sel(alu_1_result[1:0]));
  assign bit_extender_4_out = {{24{multiplexer_13_out[7]}}, multiplexer_13_out};  // Bit_Extender bit_extender_4

  // Other names for the same wires on the sheet: RegR2[31:0] = MDin

  // Notes on the sheet:
  //   中断源
  //   中断等待指示
  //   总复位信号应将除ROM以外所有存储组件全部清零
  //   数码管输出
  //   数码管输出应该用寄存器锁存，否则显示数据只能一闪而过
  //   指令存储器
  //   指令字
  //   contents of rom_1 (hex, n*v repeats v):
  //   100493 100006f 100493 200913 300993 100006f 100493 200913 300993 100006f 100493 200913 300993
  //   100006f 100493 200913 300993 29c000ef 100413 100493 1f49493 900533 2200893 73 24d493 48463 fedff06f
  //   900533 2200893 73 100493 249493 900533 2200893 73 48463 fedff06f 100493 1f49493 900533 2200893 73
  //   4034d493 900533 2200893 73 4044d493 900533 2200893 73 4044d493 900533 2200893 73 4044d493 900533
  //   2200893 73 4044d493 900533 2200893 73 4044d493 900533 2200893 73 4044d493 900533 2200893 73 4044d493
  //   900533 2200893 73 100413 1f41993 41f9d993 433 c00913 300b13 140413 f47413 800293 100313 499993
  //   89e9b3 1300533 2200893 73 406282b3 fe0294e3 140413 f00f93 1f47433 1c41413 800293 100313 49d993
  //   89e9b3 1300533 2200893 73 406282b3 fe0294e3 1c45413 406b0b33 b0463 f95ff06f 2b3 fff2c293 829293
  //   ff2e293 500533 2200893 73 fff00413 493 84a023 140413 448493 84a023 140413 448493 84a023 140413
  //   448493 84a023 140413 448493 84a023 140413 448493 84a023 140413 448493 84a023 140413 448493 84a023
  //   140413 448493 84a023 140413 448493 84a023 140413 448493 84a023 140413 448493 84a023 140413 448493
  //   84a023 140413 448493 84a023 140413 448493 84a023 140413 448493 84a023 140413 448493 140413 433
  //   3c00493 42983 4aa03 149a2b3 28663 134a023 1442023 ffc48493 fe9412e3 800533 2200893 73 440413 3c00493
  //   fc9416e3 a00893 73 413 140413 800533 2200893 73 240413 800533 2200893 73 340413 800533 2200893 73
  //   440413 800533 2200893 73 540413 800533 2200893 73 640413 800533 2200893 73 740413 800533 2200893 73
  //   840413 800533 2200893 2200893 73 8067
  //   RS1
  //   RS2
  //   RD
  //   imm12
  //   Beq
  //   Bne
  //   MemToReg
  //   MemWrite
  //   AluOP
  //   AluSrcB
  //   RegWrite
  //   SType
  //   LUI
  //   LB
  //   BLTU
  //   a7
  //   a0
  //   为方便自动评测，需要输出PC，IR，寄存器堆写如数据RDin
  //   RAM写使能MemWrite、RAM写入数据MDin等信号
  //   控制位
  //   暂停节拍，不能为0
  //   戳工具置1进入计数暂停模式，ctrl+k时钟自动运行到对应节拍暂停
  //   ctrl+k关闭时钟连续运行，将控制位置零，进入单步调试模式调试
  //   用这个时钟源需要去掉电路中的其他时钟源
  //   数据存储器
  //   可计数暂停的时钟源
endmodule

// 单周期硬布线控制器
module \单周期硬布线控制器  (
  input  [4:0] OP,
  input  [4:0] Funct,
  input  NotNop,
  output [3:0] ALU_OP,
  output RegWrite,
  output MemToReg,
  output MemWrite,
  output ALU_SRC,
  output ecall,
  output S_type,
  output Beq,
  output Bne,
  output Jalr,
  output JAL,
  output LUI,
  output LB,
  output BLTU
);

  wire \控制信号自动生成_1_regwrite ;

  \运算控制器自动生成  \u_运算控制器自动生成_1  (
    .OP2(OP[0]), .OP3(OP[1]), .OP4(OP[2]), .OP5(OP[3]), .OP6(OP[4]), .F12(Funct[0]), .F13(Funct[1]),
    .F14(Funct[2]), .F25(Funct[3]), .F30(Funct[4]), .S0(ALU_OP[0]), .S1(ALU_OP[1]), .S2(ALU_OP[2]),
    .S3(ALU_OP[3]));
  \控制信号自动生成  \u_控制信号自动生成_1  (
    .OP2(OP[0]), .OP3(OP[1]), .MemToReg(MemToReg), .OP4(OP[2]), .OP5(OP[3]), .OP6(OP[4]), .F12(Funct[0]),
    .MemWrite(MemWrite), .F13(Funct[1]), .F14(Funct[2]), .F25(Funct[3]), .F30(Funct[4]), .ALU_SRC(ALU_SRC),
    .RegWrite(\控制信号自动生成_1_regwrite ), .ecall(ecall), .S_Type(S_type), .BEQ(Beq), .BNE(Bne), .JALR(Jalr),
    .JAL(JAL), .LUI(LUI), .LB(LB), .BLTU(BLTU));
  and and_1 (RegWrite, NotNop, \控制信号自动生成_1_regwrite );

  // Other names for the same wires on the sheet: OP_CODE[4:0] = OP

  // Notes on the sheet:
  //   运算器控制器，根据指令生成运算器功能选择信号
  //   控制信号生成，产生数据通路需要的其他控制信号
endmodule

// 运算器控制器
module \运算控制器自动生成  (
  input  OP2,
  input  OP3,
  input  OP4,
  input  OP5,
  input  OP6,
  input  F12,
  input  F13,
  input  F14,
  input  F25,
  input  F30,
  output S0,
  output S1,
  output S2,
  output S3
);

  wire and_1_out, and_2_out, and_3_out, and_4_out, and_5_out, and_6_out, and_7_out, and_8_out, and_9_out,
       and_10_out, and_11_out, and_12_out, and_13_out, and_14_out, and_15_out, and_16_out, and_17_out,
       and_18_out, and_19_out, and_20_out, and_21_out, and_22_out, and_23_out, and_24_out, and_25_out,
       and_26_out, and_27_out, and_28_out, and_29_out, and_30_out, and_31_out, and_32_out, and_33_out,
       and_34_out, and_35_out, not_1_out, not_2_out, not_3_out, not_4_out, not_5_out, not_6_out, not_7_out,
       not_8_out, not_9_out, not_10_out, not_11_out, not_12_out, not_13_out, not_14_out, not_15_out,
       not_16_out, not_17_out, not_18_out, not_19_out, not_20_out, not_21_out, not_22_out, not_23_out,
       not_24_out, not_25_out, not_26_out, not_27_out, not_28_out, not_29_out, not_30_out, not_31_out,
       not_32_out, not_33_out, not_34_out, not_35_out, not_36_out, not_37_out, not_38_out, not_39_out,
       not_40_out, not_41_out, not_42_out, not_43_out, not_44_out, not_45_out, not_46_out, not_47_out,
       not_48_out, not_49_out, not_50_out, not_51_out, not_52_out, not_53_out, not_54_out, not_55_out,
       not_56_out, not_57_out, not_58_out, not_59_out, not_60_out, not_61_out, not_62_out, not_63_out,
       not_64_out, not_65_out, not_66_out, not_67_out, not_68_out, not_69_out, not_70_out, not_71_out,
       not_72_out, not_73_out, not_74_out, not_75_out, not_76_out, not_77_out, not_78_out, not_79_out,
       not_80_out, not_81_out, not_82_out, not_83_out, not_84_out, not_85_out, not_86_out, not_87_out,
       not_88_out, not_89_out, not_90_out, not_91_out, not_92_out, not_93_out, not_94_out, not_95_out,
       not_96_out, not_97_out, not_98_out, not_99_out, not_100_out, not_101_out, not_102_out, not_103_out,
       not_104_out, not_105_out, not_106_out, not_107_out, not_108_out, not_109_out, not_110_out,
       not_111_out, not_112_out, not_113_out, not_114_out, not_115_out, not_116_out, not_117_out,
       not_118_out, not_119_out, not_120_out, not_121_out, not_122_out, not_123_out, not_124_out,
       not_125_out, not_126_out, not_127_out, not_128_out, not_129_out, not_130_out, not_131_out,
       not_132_out, not_133_out, not_134_out, not_135_out, not_136_out, not_137_out, not_138_out,
       not_139_out, not_140_out, not_141_out, not_142_out, not_143_out, not_144_out, not_145_out,
       not_146_out, not_147_out, not_148_out, not_149_out, not_150_out, not_151_out, not_152_out,
       not_153_out, not_154_out, not_155_out, not_156_out, not_157_out, not_158_out, not_159_out,
       not_160_out, not_161_out, not_162_out, not_163_out, not_164_out, not_165_out, not_166_out,
       not_167_out, not_168_out, not_169_out, not_170_out, not_171_out, not_172_out, not_173_out,
       not_174_out, not_175_out, not_176_out, not_177_out, not_178_out, not_179_out, not_180_out,
       not_181_out, not_182_out, not_183_out, not_184_out, not_185_out, not_186_out, not_187_out,
       not_188_out, not_189_out, not_190_out, not_191_out, not_192_out, not_193_out, not_194_out,
       not_195_out, not_196_out, not_197_out, not_198_out, not_199_out, not_200_out, not_201_out,
       not_202_out, not_203_out, not_204_out, not_205_out, not_206_out, not_207_out, not_208_out,
       not_209_out, not_210_out, not_211_out, not_212_out, not_213_out, not_214_out;

  not not_1 (not_1_out, F30);
  not not_2 (not_2_out, F25);
  not not_3 (not_3_out, F14);
  not not_4 (not_4_out, F13);
  not not_5 (not_5_out, F12);
  not not_6 (not_6_out, OP6);
  not not_7 (not_7_out, OP3);
  not not_8 (not_8_out, OP2);
  not not_9 (not_9_out, F30);
  not not_10 (not_10_out, F25);
  not not_11 (not_11_out, OP6);
  not not_12 (not_12_out, OP3);
  not not_13 (not_13_out, OP2);
  not not_14 (not_14_out, F30);
  not not_15 (not_15_out, F25);
  not not_16 (not_16_out, F14);
  not not_17 (not_17_out, F12);
  not not_18 (not_18_out, OP6);
  not not_19 (not_19_out, OP3);
  not not_20 (not_20_out, OP2);
  not not_21 (not_21_out, F14);
  not not_22 (not_22_out, F13);
  not not_23 (not_23_out, F12);
  not not_24 (not_24_out, OP6);
  not not_25 (not_25_out, OP5);
  not not_26 (not_26_out, OP3);
  not not_27 (not_27_out, OP2);
  not not_28 (not_28_out, OP6);
  not not_29 (not_29_out, OP5);
  not not_30 (not_30_out, OP3);
  not not_31 (not_31_out, OP2);
  not not_32 (not_32_out, F13);
  not not_33 (not_33_out, F12);
  not not_34 (not_34_out, OP6);
  not not_35 (not_35_out, OP5);
  not not_36 (not_36_out, OP3);
  not not_37 (not_37_out, OP2);
  not not_38 (not_38_out, F14);
  not not_39 (not_39_out, F12);
  not not_40 (not_40_out, OP6);
  not not_41 (not_41_out, OP5);
  not not_42 (not_42_out, OP3);
  not not_43 (not_43_out, OP2);
  not not_44 (not_44_out, F25);
  not not_45 (not_45_out, F13);
  not not_46 (not_46_out, OP6);
  not not_47 (not_47_out, OP5);
  not not_48 (not_48_out, OP3);
  not not_49 (not_49_out, OP2);
  not not_50 (not_50_out, F14);
  not not_51 (not_51_out, F12);
  not not_52 (not_52_out, OP6);
  not not_53 (not_53_out, OP5);
  not not_54 (not_54_out, OP4);
  not not_55 (not_55_out, OP3);
  not not_56 (not_56_out, OP2);
  not not_57 (not_57_out, F14);
  not not_58 (not_58_out, F12);
  not not_59 (not_59_out, OP6);
  not not_60 (not_60_out, OP4);
  not not_61 (not_61_out, OP3);
  not not_62 (not_62_out, OP2);
  not not_63 (not_63_out, F14);
  not not_64 (not_64_out, F13);
  not not_65 (not_65_out, F12);
  not not_66 (not_66_out, OP6);
  not not_67 (not_67_out, OP5);
  not not_68 (not_68_out, OP4);
  not not_69 (not_69_out, OP3);
  not not_70 (not_70_out, OP2);
  not not_71 (not_71_out, F25);
  not not_72 (not_72_out, F14);
  not not_73 (not_73_out, F13);
  not not_74 (not_74_out, F12);
  not not_75 (not_75_out, OP6);
  not not_76 (not_76_out, OP3);
  not not_77 (not_77_out, OP2);
  not not_78 (not_78_out, F30);
  not not_79 (not_79_out, F25);
  not not_80 (not_80_out, OP6);
  not not_81 (not_81_out, OP3);
  not not_82 (not_82_out, OP2);
  not not_83 (not_83_out, F30);
  not not_84 (not_84_out, F25);
  not not_85 (not_85_out, F14);
  not not_86 (not_86_out, F12);
  not not_87 (not_87_out, OP6);
  not not_88 (not_88_out, OP3);
  not not_89 (not_89_out, OP2);
  not not_90 (not_90_out, OP6);
  not not_91 (not_91_out, OP5);
  not not_92 (not_92_out, OP3);
  not not_93 (not_93_out, OP2);
  not not_94 (not_94_out, F14);
  not not_95 (not_95_out, F12);
  not not_96 (not_96_out, OP6);
  not not_97 (not_97_out, OP5);
  not not_98 (not_98_out, OP3);
  not not_99 (not_99_out, OP2);
  not not_100 (not_100_out, F30);
  not not_101 (not_101_out, F25);
  not not_102 (not_102_out, F13);
  not not_103 (not_103_out, OP6);
  not not_104 (not_104_out, OP5);
  not not_105 (not_105_out, OP3);
  not not_106 (not_106_out, OP2);
  not not_107 (not_107_out, F30);
  not not_108 (not_108_out, F25);
  not not_109 (not_109_out, F13);
  not not_110 (not_110_out, OP6);
  not not_111 (not_111_out, OP3);
  not not_112 (not_112_out, OP2);
  not not_113 (not_113_out, F30);
  not not_114 (not_114_out, F25);
  not not_115 (not_115_out, F14);
  not not_116 (not_116_out, F13);
  not not_117 (not_117_out, F12);
  not not_118 (not_118_out, OP6);
  not not_119 (not_119_out, OP3);
  not not_120 (not_120_out, OP2);
  not not_121 (not_121_out, F25);
  not not_122 (not_122_out, F14);
  not not_123 (not_123_out, F13);
  not not_124 (not_124_out, F12);
  not not_125 (not_125_out, OP6);
  not not_126 (not_126_out, OP3);
  not not_127 (not_127_out, OP2);
  not not_128 (not_128_out, F30);
  not not_129 (not_129_out, F25);
  not not_130 (not_130_out, OP6);
  not not_131 (not_131_out, OP3);
  not not_132 (not_132_out, OP2);
  not not_133 (not_133_out, F30);
  not not_134 (not_134_out, F25);
  not not_135 (not_135_out, F14);
  not not_136 (not_136_out, OP6);
  not not_137 (not_137_out, OP3);
  not not_138 (not_138_out, OP2);
  not not_139 (not_139_out, F14);
  not not_140 (not_140_out, F13);
  not not_141 (not_141_out, F12);
  not not_142 (not_142_out, OP6);
  not not_143 (not_143_out, OP5);
  not not_144 (not_144_out, OP3);
  not not_145 (not_145_out, OP2);
  not not_146 (not_146_out, OP6);
  not not_147 (not_147_out, OP5);
  not not_148 (not_148_out, OP3);
  not not_149 (not_149_out, OP2);
  not not_150 (not_150_out, F14);
  not not_151 (not_151_out, F12);
  not not_152 (not_152_out, OP6);
  not not_153 (not_153_out, OP5);
  not not_154 (not_154_out, OP4);
  not not_155 (not_155_out, OP3);
  not not_156 (not_156_out, OP2);
  not not_157 (not_157_out, F14);
  not not_158 (not_158_out, F12);
  not not_159 (not_159_out, OP6);
  not not_160 (not_160_out, OP4);
  not not_161 (not_161_out, OP3);
  not not_162 (not_162_out, OP2);
  not not_163 (not_163_out, F14);
  not not_164 (not_164_out, F13);
  not not_165 (not_165_out, F12);
  not not_166 (not_166_out, OP6);
  not not_167 (not_167_out, OP5);
  not not_168 (not_168_out, OP4);
  not not_169 (not_169_out, OP3);
  not not_170 (not_170_out, OP2);
  not not_171 (not_171_out, F12);
  not not_172 (not_172_out, OP4);
  not not_173 (not_173_out, OP3);
  not not_174 (not_174_out, OP2);
  not not_175 (not_175_out, F30);
  not not_176 (not_176_out, F25);
  not not_177 (not_177_out, F12);
  not not_178 (not_178_out, OP6);
  not not_179 (not_179_out, OP3);
  not not_180 (not_180_out, OP2);
  not not_181 (not_181_out, F30);
  not not_182 (not_182_out, F25);
  not not_183 (not_183_out, F14);
  not not_184 (not_184_out, F12);
  not not_185 (not_185_out, OP6);
  not not_186 (not_186_out, OP3);
  not not_187 (not_187_out, OP2);
  not not_188 (not_188_out, F30);
  not not_189 (not_189_out, F25);
  not not_190 (not_190_out, F14);
  not not_191 (not_191_out, OP6);
  not not_192 (not_192_out, OP3);
  not not_193 (not_193_out, OP2);
  not not_194 (not_194_out, F12);
  not not_195 (not_195_out, OP6);
  not not_196 (not_196_out, OP5);
  not not_197 (not_197_out, OP3);
  not not_198 (not_198_out, OP2);
  not not_199 (not_199_out, F13);
  not not_200 (not_200_out, F12);
  not not_201 (not_201_out, OP6);
  not not_202 (not_202_out, OP5);
  not not_203 (not_203_out, OP3);
  not not_204 (not_204_out, OP2);
  not not_205 (not_205_out, F14);
  not not_206 (not_206_out, F12);
  not not_207 (not_207_out, OP6);
  not not_208 (not_208_out, OP5);
  not not_209 (not_209_out, OP3);
  not not_210 (not_210_out, OP2);
  not not_211 (not_211_out, F12);
  not not_212 (not_212_out, OP4);
  not not_213 (not_213_out, OP3);
  not not_214 (not_214_out, OP2);
  and and_1 (and_1_out, not_1_out, not_2_out, not_3_out, not_4_out, not_5_out, not_6_out, OP5, OP4, not_7_out, not_8_out);
  and and_2 (and_2_out, not_9_out, not_10_out, F14, F13, F12, not_11_out, OP5, OP4, not_12_out, not_13_out);
  and and_3 (and_3_out, not_14_out, not_15_out, not_16_out, F13, not_17_out, not_18_out, OP5, OP4, not_19_out, not_20_out);
  and and_4 (and_4_out, not_21_out, not_22_out, not_23_out, not_24_out, not_25_out, OP4, not_26_out, not_27_out);
  and and_5 (and_5_out, F14, F13, F12, not_28_out, not_29_out, OP4, not_30_out, not_31_out);
  and and_6 (and_6_out, F14, not_32_out, not_33_out, not_34_out, not_35_out, OP4, not_36_out, not_37_out);
  and and_7 (and_7_out, not_38_out, F13, not_39_out, not_40_out, not_41_out, OP4, not_42_out, not_43_out);
  and and_8 (and_8_out, F30, not_44_out, F14, not_45_out, F12, not_46_out, not_47_out, OP4, not_48_out, not_49_out);
  and and_9 (and_9_out, not_50_out, F13, not_51_out, not_52_out, not_53_out, not_54_out, not_55_out, not_56_out);
  and and_10 (and_10_out, not_57_out, F13, not_58_out, not_59_out, OP5, not_60_out, not_61_out, not_62_out);
  and and_11 (and_11_out, not_63_out, not_64_out, not_65_out, not_66_out, not_67_out, not_68_out, not_69_out, not_70_out);
  and and_12 (and_12_out, F30, not_71_out, not_72_out, not_73_out, not_74_out, not_75_out, OP5, OP4, not_76_out, not_77_out);
  and and_13 (and_13_out, not_78_out, not_79_out, F14, F13, F12, not_80_out, OP5, OP4, not_81_out, not_82_out);
  and and_14 (and_14_out, not_83_out, not_84_out, not_85_out, F13, not_86_out, not_87_out, OP5, OP4, not_88_out, not_89_out);
  and and_15 (and_15_out, F14, F13, F12, not_90_out, not_91_out, OP4, not_92_out, not_93_out);
  and and_16 (and_16_out, not_94_out, F13, not_95_out, not_96_out, not_97_out, OP4, not_98_out, not_99_out);
  and and_17 (and_17_out, not_100_out, not_101_out, F14, not_102_out, F12, not_103_out, not_104_out, OP4, not_105_out, not_106_out);
  and and_18 (and_18_out, not_107_out, not_108_out, F14, not_109_out, F12, not_110_out, OP5, OP4, not_111_out, not_112_out);
  and and_19 (and_19_out, not_113_out, not_114_out, not_115_out, not_116_out, not_117_out, not_118_out, OP5, OP4, not_119_out, not_120_out);
  and and_20 (and_20_out, F30, not_121_out, not_122_out, not_123_out, not_124_out, not_125_out, OP5, OP4, not_126_out, not_127_out);
  and and_21 (and_21_out, not_128_out, not_129_out, F14, F13, F12, not_130_out, OP5, OP4, not_131_out, not_132_out);
  and and_22 (and_22_out, not_133_out, not_134_out, not_135_out, F13, F12, not_136_out, OP5, OP4, not_137_out, not_138_out);
  and and_23 (and_23_out, not_139_out, not_140_out, not_141_out, not_142_out, not_143_out, OP4, not_144_out, not_145_out);
  and and_24 (and_24_out, F14, F13, F12, not_146_out, not_147_out, OP4, not_148_out, not_149_out);
  and and_25 (and_25_out, not_150_out, F13, not_151_out, not_152_out, not_153_out, not_154_out, not_155_out, not_156_out);
  and and_26 (and_26_out, not_157_out, F13, not_158_out, not_159_out, OP5, not_160_out, not_161_out, not_162_out);
  and and_27 (and_27_out, not_163_out, not_164_out, not_165_out, not_166_out, not_167_out, not_168_out, not_169_out, not_170_out);
  and and_28 (and_28_out, F14, F13, not_171_out, OP6, OP5, not_172_out, not_173_out, not_174_out);
  and and_29 (and_29_out, not_175_out, not_176_out, F14, F13, not_177_out, not_178_out, OP5, OP4, not_179_out, not_180_out);
  and and_30 (and_30_out, not_181_out, not_182_out, not_183_out, F13, not_184_out, not_185_out, OP5, OP4, not_186_out, not_187_out);
  and and_31 (and_31_out, not_188_out, not_189_out, not_190_out, F13, F12, not_191_out, OP5, OP4, not_192_out, not_193_out);
  and and_32 (and_32_out, F14, F13, not_194_out, not_195_out, not_196_out, OP4, not_197_out, not_198_out);
  and and_33 (and_33_out, F14, not_199_out, not_200_out, not_201_out, not_202_out, OP4, not_203_out, not_204_out);
  and and_34 (and_34_out, not_205_out, F13, not_206_out, not_207_out, not_208_out, OP4, not_209_out, not_210_out);
  and and_35 (and_35_out, F14, F13, not_211_out, OP6, OP5, not_212_out, not_213_out, not_214_out);
  or or_1 (S0, and_1_out, and_2_out, and_3_out, and_4_out, and_5_out, and_6_out, and_7_out, and_8_out, and_9_out, and_10_out, and_11_out);
  or or_2 (S1, and_12_out, and_13_out, and_14_out, and_15_out, and_16_out, and_17_out, and_18_out);
  or or_3 (S2, and_19_out, and_20_out, and_21_out, and_22_out, and_23_out, and_24_out, and_25_out, and_26_out, and_27_out, and_28_out);
  or or_4 (S3, and_29_out, and_30_out, and_31_out, and_32_out, and_33_out, and_34_out, and_35_out);
endmodule

// 控制信号生成
module \控制信号自动生成  (
  input  OP2,
  input  OP3,
  input  OP4,
  input  OP5,
  input  OP6,
  input  F12,
  input  F13,
  input  F14,
  input  F25,
  input  F30,
  output MemToReg,
  output MemWrite,
  output ALU_SRC,
  output RegWrite,
  output ecall,
  output S_Type,
  output BEQ,
  output BNE,
  output JALR,
  output JAL,
  output LUI,
  output LB,
  output BLTU
);

  wire and_3_out, and_4_out, and_5_out, and_6_out, and_7_out, and_8_out, and_9_out, and_10_out, and_11_out,
       and_12_out, and_13_out, and_14_out, and_15_out, and_16_out, and_17_out, and_18_out, and_19_out,
       and_20_out, and_21_out, and_22_out, and_23_out, and_24_out, and_25_out, and_26_out, and_27_out,
       and_28_out, not_1_out, not_2_out, not_3_out, not_4_out, not_5_out, not_6_out, not_7_out, not_8_out,
       not_9_out, not_10_out, not_11_out, not_12_out, not_13_out, not_14_out, not_15_out, not_16_out,
       not_17_out, not_18_out, not_19_out, not_20_out, not_21_out, not_22_out, not_23_out, not_24_out,
       not_25_out, not_26_out, not_27_out, not_28_out, not_29_out, not_30_out, not_31_out, not_32_out,
       not_33_out, not_34_out, not_35_out, not_36_out, not_37_out, not_38_out, not_39_out, not_40_out,
       not_41_out, not_42_out, not_43_out, not_44_out, not_45_out, not_46_out, not_47_out, not_48_out,
       not_49_out, not_50_out, not_51_out, not_52_out, not_53_out, not_54_out, not_55_out, not_56_out,
       not_57_out, not_58_out, not_59_out, not_60_out, not_61_out, not_62_out, not_63_out, not_64_out,
       not_65_out, not_66_out, not_67_out, not_68_out, not_69_out, not_70_out, not_71_out, not_72_out,
       not_73_out, not_74_out, not_75_out, not_76_out, not_77_out, not_78_out, not_79_out, not_80_out,
       not_81_out, not_82_out, not_83_out, not_84_out, not_85_out, not_86_out, not_87_out, not_88_out,
       not_89_out, not_90_out, not_91_out, not_92_out, not_93_out, not_94_out, not_95_out, not_96_out,
       not_97_out, not_98_out, not_99_out, not_100_out, not_101_out, not_102_out, not_103_out, not_104_out,
       not_105_out, not_106_out, not_107_out, not_108_out, not_109_out, not_110_out, not_111_out,
       not_112_out, not_113_out, not_114_out, not_115_out, not_116_out, not_117_out, not_118_out,
       not_119_out, not_120_out, not_121_out, not_122_out, not_123_out, not_124_out, not_125_out,
       not_126_out, not_127_out, not_128_out, not_129_out, not_130_out, not_131_out, not_132_out,
       not_133_out, not_134_out, not_135_out, not_136_out, not_137_out, not_138_out, not_139_out,
       not_140_out, not_141_out, not_142_out, not_143_out, not_144_out, not_145_out, not_146_out,
       not_147_out, not_148_out, not_149_out, not_150_out, not_151_out, not_152_out, not_153_out,
       not_154_out, not_155_out, not_156_out, not_157_out, not_158_out, not_159_out, not_160_out,
       not_161_out, not_162_out, not_163_out, not_164_out, not_165_out, not_166_out, not_167_out,
       not_168_out, not_169_out, not_170_out, not_171_out, not_172_out, not_173_out, not_174_out,
       not_175_out, not_176_out, not_177_out, not_178_out, not_179_out, not_180_out, not_181_out,
       not_182_out, not_183_out, not_184_out, not_185_out, not_186_out, not_187_out, not_188_out,
       not_189_out, not_190_out, not_191_out, not_192_out, not_193_out, not_194_out, not_195_out,
       not_196_out, not_197_out, not_198_out, not_199_out, not_200_out, not_201_out, not_202_out,
       not_203_out, not_204_out, not_205_out, not_206_out, not_207_out;

  not not_1 (not_1_out, OP2);
  not not_2 (not_2_out, OP3);
  not not_3 (not_3_out, OP4);
  not not_4 (not_4_out, OP5);
  not not_5 (not_5_out, OP6);
  not not_6 (not_6_out, F12);
  not not_7 (not_7_out, F14);
  not not_8 (not_8_out, OP2);
  not not_9 (not_9_out, OP3);
  not not_10 (not_10_out, OP4);
  not not_11 (not_11_out, OP6);
  not not_12 (not_12_out, F12);
  not not_13 (not_13_out, F14);
  not not_14 (not_14_out, OP2);
  not not_15 (not_15_out, OP3);
  not not_16 (not_16_out, OP5);
  not not_17 (not_17_out, OP6);
  not not_18 (not_18_out, F12);
  not not_19 (not_19_out, F14);
  not not_20 (not_20_out, OP2);
  not not_21 (not_21_out, OP3);
  not not_22 (not_22_out, OP4);
  not not_23 (not_23_out, OP6);
  not not_24 (not_24_out, F12);
  not not_25 (not_25_out, F14);
  not not_26 (not_26_out, OP2);
  not not_27 (not_27_out, OP3);
  not not_28 (not_28_out, OP5);
  not not_29 (not_29_out, OP6);
  not not_30 (not_30_out, F12);
  not not_31 (not_31_out, OP2);
  not not_32 (not_32_out, OP3);
  not not_33 (not_33_out, OP5);
  not not_34 (not_34_out, OP6);
  not not_35 (not_35_out, F13);
  not not_36 (not_36_out, F25);
  not not_37 (not_37_out, F30);
  not not_38 (not_38_out, OP2);
  not not_39 (not_39_out, OP3);
  not not_40 (not_40_out, OP5);
  not not_41 (not_41_out, OP6);
  not not_42 (not_42_out, F25);
  not not_43 (not_43_out, OP2);
  not not_44 (not_44_out, OP3);
  not not_45 (not_45_out, OP5);
  not not_46 (not_46_out, OP6);
  not not_47 (not_47_out, F30);
  not not_48 (not_48_out, F25);
  not not_49 (not_49_out, F14);
  not not_50 (not_50_out, F13);
  not not_51 (not_51_out, F12);
  not not_52 (not_52_out, OP6);
  not not_53 (not_53_out, OP3);
  not not_54 (not_54_out, OP2);
  not not_55 (not_55_out, F25);
  not not_56 (not_56_out, F14);
  not not_57 (not_57_out, F13);
  not not_58 (not_58_out, F12);
  not not_59 (not_59_out, OP6);
  not not_60 (not_60_out, OP3);
  not not_61 (not_61_out, OP2);
  not not_62 (not_62_out, F30);
  not not_63 (not_63_out, F25);
  not not_64 (not_64_out, OP6);
  not not_65 (not_65_out, OP3);
  not not_66 (not_66_out, OP2);
  not not_67 (not_67_out, F30);
  not not_68 (not_68_out, F25);
  not not_69 (not_69_out, F12);
  not not_70 (not_70_out, OP6);
  not not_71 (not_71_out, OP3);
  not not_72 (not_72_out, OP2);
  not not_73 (not_73_out, F30);
  not not_74 (not_74_out, F25);
  not not_75 (not_75_out, F14);
  not not_76 (not_76_out, F12);
  not not_77 (not_77_out, OP6);
  not not_78 (not_78_out, OP3);
  not not_79 (not_79_out, OP2);
  not not_80 (not_80_out, F30);
  not not_81 (not_81_out, F25);
  not not_82 (not_82_out, F14);
  not not_83 (not_83_out, OP6);
  not not_84 (not_84_out, OP3);
  not not_85 (not_85_out, OP2);
  not not_86 (not_86_out, F14);
  not not_87 (not_87_out, F13);
  not not_88 (not_88_out, F12);
  not not_89 (not_89_out, OP6);
  not not_90 (not_90_out, OP5);
  not not_91 (not_91_out, OP3);
  not not_92 (not_92_out, OP2);
  not not_93 (not_93_out, OP6);
  not not_94 (not_94_out, OP5);
  not not_95 (not_95_out, OP3);
  not not_96 (not_96_out, OP2);
  not not_97 (not_97_out, F12);
  not not_98 (not_98_out, OP6);
  not not_99 (not_99_out, OP5);
  not not_100 (not_100_out, OP3);
  not not_101 (not_101_out, OP2);
  not not_102 (not_102_out, F13);
  not not_103 (not_103_out, F12);
  not not_104 (not_104_out, OP6);
  not not_105 (not_105_out, OP5);
  not not_106 (not_106_out, OP3);
  not not_107 (not_107_out, OP2);
  not not_108 (not_108_out, F14);
  not not_109 (not_109_out, F12);
  not not_110 (not_110_out, OP6);
  not not_111 (not_111_out, OP5);
  not not_112 (not_112_out, OP3);
  not not_113 (not_113_out, OP2);
  not not_114 (not_114_out, F30);
  not not_115 (not_115_out, F25);
  not not_116 (not_116_out, F14);
  not not_117 (not_117_out, F13);
  not not_118 (not_118_out, OP6);
  not not_119 (not_119_out, OP5);
  not not_120 (not_120_out, OP3);
  not not_121 (not_121_out, OP2);
  not not_122 (not_122_out, F30);
  not not_123 (not_123_out, F25);
  not not_124 (not_124_out, F13);
  not not_125 (not_125_out, OP6);
  not not_126 (not_126_out, OP5);
  not not_127 (not_127_out, OP3);
  not not_128 (not_128_out, OP2);
  not not_129 (not_129_out, F25);
  not not_130 (not_130_out, F13);
  not not_131 (not_131_out, OP6);
  not not_132 (not_132_out, OP5);
  not not_133 (not_133_out, OP3);
  not not_134 (not_134_out, OP2);
  not not_135 (not_135_out, F14);
  not not_136 (not_136_out, F12);
  not not_137 (not_137_out, OP6);
  not not_138 (not_138_out, OP5);
  not not_139 (not_139_out, OP4);
  not not_140 (not_140_out, OP3);
  not not_141 (not_141_out, OP2);
  not not_142 (not_142_out, OP4);
  not not_143 (not_143_out, F14);
  not not_144 (not_144_out, F13);
  not not_145 (not_145_out, F12);
  not not_146 (not_146_out, OP4);
  not not_147 (not_147_out, OP3);
  not not_148 (not_148_out, F30);
  not not_149 (not_149_out, F25);
  not not_150 (not_150_out, F13);
  not not_151 (not_151_out, OP6);
  not not_152 (not_152_out, OP3);
  not not_153 (not_153_out, OP2);
  not not_154 (not_154_out, OP6);
  not not_155 (not_155_out, OP3);
  not not_156 (not_156_out, F14);
  not not_157 (not_157_out, F13);
  not not_158 (not_158_out, F12);
  not not_159 (not_159_out, OP6);
  not not_160 (not_160_out, OP5);
  not not_161 (not_161_out, OP4);
  not not_162 (not_162_out, OP3);
  not not_163 (not_163_out, OP2);
  not not_164 (not_164_out, OP2);
  not not_165 (not_165_out, OP3);
  not not_166 (not_166_out, F12);
  not not_167 (not_167_out, F13);
  not not_168 (not_168_out, F14);
  not not_169 (not_169_out, F25);
  not not_170 (not_170_out, F30);
  not not_171 (not_171_out, OP2);
  not not_172 (not_172_out, OP3);
  not not_173 (not_173_out, OP4);
  not not_174 (not_174_out, OP6);
  not not_175 (not_175_out, F12);
  not not_176 (not_176_out, F14);
  not not_177 (not_177_out, OP2);
  not not_178 (not_178_out, OP3);
  not not_179 (not_179_out, OP4);
  not not_180 (not_180_out, F12);
  not not_181 (not_181_out, F13);
  not not_182 (not_182_out, F14);
  not not_183 (not_183_out, OP2);
  not not_184 (not_184_out, OP3);
  not not_185 (not_185_out, OP4);
  not not_186 (not_186_out, F13);
  not not_187 (not_187_out, F14);
  not not_188 (not_188_out, OP3);
  not not_189 (not_189_out, OP4);
  not not_190 (not_190_out, F12);
  not not_191 (not_191_out, F13);
  not not_192 (not_192_out, F14);
  not not_193 (not_193_out, OP4);
  not not_194 (not_194_out, OP3);
  not not_195 (not_195_out, OP6);
  not not_196 (not_196_out, OP2);
  not not_197 (not_197_out, OP3);
  not not_198 (not_198_out, OP4);
  not not_199 (not_199_out, OP5);
  not not_200 (not_200_out, OP6);
  not not_201 (not_201_out, F12);
  not not_202 (not_202_out, F13);
  not not_203 (not_203_out, F14);
  not not_204 (not_204_out, OP2);
  not not_205 (not_205_out, OP3);
  not not_206 (not_206_out, OP4);
  not not_207 (not_207_out, F12);
  and and_1 (MemToReg, not_1_out, not_2_out, not_3_out, not_4_out, not_5_out, not_6_out, not_7_out);
  and and_2 (MemWrite, not_8_out, not_9_out, not_10_out, OP5, not_11_out, not_12_out, F13, not_13_out);
  and and_3 (and_3_out, not_14_out, not_15_out, not_16_out, not_17_out, not_18_out, not_19_out);
  and and_4 (and_4_out, not_20_out, not_21_out, not_22_out, not_23_out, not_24_out, F13, not_25_out);
  and and_5 (and_5_out, not_26_out, not_27_out, OP4, not_28_out, not_29_out, not_30_out);
  and and_6 (and_6_out, not_31_out, not_32_out, OP4, not_33_out, not_34_out, not_35_out, not_36_out, not_37_out);
  and and_7 (and_7_out, not_38_out, not_39_out, OP4, not_40_out, not_41_out, F14, not_42_out);
  and and_8 (and_8_out, not_43_out, not_44_out, OP4, not_45_out, not_46_out, F13, F14);
  and and_9 (and_9_out, not_47_out, not_48_out, not_49_out, not_50_out, not_51_out, not_52_out, OP5, OP4, not_53_out, not_54_out);
  and and_10 (and_10_out, F30, not_55_out, not_56_out, not_57_out, not_58_out, not_59_out, OP5, OP4, not_60_out, not_61_out);
  and and_11 (and_11_out, not_62_out, not_63_out, F14, F13, F12, not_64_out, OP5, OP4, not_65_out, not_66_out);
  and and_12 (and_12_out, not_67_out, not_68_out, F14, F13, not_69_out, not_70_out, OP5, OP4, not_71_out, not_72_out);
  and and_13 (and_13_out, not_73_out, not_74_out, not_75_out, F13, not_76_out, not_77_out, OP5, OP4, not_78_out, not_79_out);
  and and_14 (and_14_out, not_80_out, not_81_out, not_82_out, F13, F12, not_83_out, OP5, OP4, not_84_out, not_85_out);
  and and_15 (and_15_out, not_86_out, not_87_out, not_88_out, not_89_out, not_90_out, OP4, not_91_out, not_92_out);
  and and_16 (and_16_out, F14, F13, F12, not_93_out, not_94_out, OP4, not_95_out, not_96_out);
  and and_17 (and_17_out, F14, F13, not_97_out, not_98_out, not_99_out, OP4, not_100_out, not_101_out);
  and and_18 (and_18_out, F14, not_102_out, not_103_out, not_104_out, not_105_out, OP4, not_106_out, not_107_out);
  and and_19 (and_19_out, not_108_out, F13, not_109_out, not_110_out, not_111_out, OP4, not_112_out, not_113_out);
  and and_20 (and_20_out, not_114_out, not_115_out, not_116_out, not_117_out, F12, not_118_out, not_119_out, OP4, not_120_out, not_121_out);
  and and_21 (and_21_out, not_122_out, not_123_out, F14, not_124_out, F12, not_125_out, not_126_out, OP4, not_127_out, not_128_out);
  and and_22 (and_22_out, F30, not_129_out, F14, not_130_out, F12, not_131_out, not_132_out, OP4, not_133_out, not_134_out);
  and and_23 (and_23_out, not_135_out, F13, not_136_out, not_137_out, not_138_out, not_139_out, not_140_out, not_141_out);
  and and_24 (and_24_out, OP6, OP5, not_142_out, OP3, OP2);
  and and_25 (and_25_out, not_143_out, not_144_out, not_145_out, OP6, OP5, not_146_out, not_147_out, OP2);
  and and_26 (and_26_out, not_148_out, not_149_out, F14, not_150_out, F12, not_151_out, OP5, OP4, not_152_out, not_153_out);
  and and_27 (and_27_out, not_154_out, OP5, OP4, not_155_out, OP2);
  and and_28 (and_28_out, not_156_out, not_157_out, not_158_out, not_159_out, not_160_out, not_161_out, not_162_out, not_163_out);
  and and_29 (ecall, not_164_out, not_165_out, OP4, OP5, OP6, not_166_out, not_167_out, not_168_out, not_169_out, not_170_out);
  and and_30 (S_Type, not_171_out, not_172_out, not_173_out, OP5, not_174_out, not_175_out, F13, not_176_out);
  and and_31 (BEQ, not_177_out, not_178_out, not_179_out, OP5, OP6, not_180_out, not_181_out, not_182_out);
  and and_32 (BNE, not_183_out, not_184_out, not_185_out, OP5, OP6, F12, not_186_out, not_187_out);
  and and_33 (JALR, OP2, not_188_out, not_189_out, OP5, OP6, not_190_out, not_191_out, not_192_out);
  and and_34 (JAL, OP2, OP3, not_193_out, OP5, OP6);
  and and_35 (LUI, OP2, not_194_out, OP4, OP5, not_195_out);
  and and_36 (LB, not_196_out, not_197_out, not_198_out, not_199_out, not_200_out, not_201_out, not_202_out, not_203_out);
  and and_37 (BLTU, not_204_out, not_205_out, not_206_out, OP5, OP6, not_207_out, F13, F14);
  or or_1 (ALU_SRC, and_3_out, and_4_out, and_5_out, and_6_out, and_7_out, and_8_out);
  or or_2 (RegWrite, and_9_out, and_10_out, and_11_out, and_12_out, and_13_out, and_14_out, and_15_out, and_16_out, and_17_out, and_18_out, and_19_out, and_20_out, and_21_out, and_22_out, and_23_out, and_24_out, and_25_out, and_26_out, and_27_out, and_28_out);
endmodule

// ALU
module ALU (
  input  [31:0] X,
  input  [31:0] Y,
  input  [3:0] AluOP,
  output out_4,
  output Equal,
  output out_6,
  output [31:0] Result,
  output [31:0] Result_2
);

  wire [0:0] comparator_1_lt, comparator_2_lt;
  wire [31:0] adder_1_out, AND_out, divider_1_out, divider_1_rem, multiplier_1_cout, multiplier_1_out,
       NOR_out, OR_out, shifter_1_out, shifter_2_out, shifter_3_out, subtractor_1_out, XOR_out;

  assign AND_out = X & Y;  // AND_Gate AND, 32 bits wide
  assign OR_out = X | Y;  // OR_Gate OR, 32 bits wide
  Shifter #(.width(32), .shift("ll")) shifter_1 (.in(X), .\dist (Y[4:0]), .out(shifter_1_out));
  Shifter #(.width(32), .shift("ar")) shifter_2 (.in(X), .\dist (Y[4:0]), .out(shifter_2_out));
  Shifter #(.width(32), .shift("lr")) shifter_3 (.in(X), .\dist (Y[4:0]), .out(shifter_3_out));
  Multiplier #(.width(32)) multiplier_1 (.a(X), .b(Y), .out(multiplier_1_out), .cout(multiplier_1_cout));  // open: cin
  Divider #(.width(32)) divider_1 (.a(X), .b(Y), .out(divider_1_out), .rem(divider_1_rem));  // open: upper
  Adder #(.width(32)) adder_1 (.a(X), .b(Y), .out(adder_1_out));  // open: cin, cout
  Subtractor #(.width(32)) subtractor_1 (.a(X), .b(Y), .out(subtractor_1_out));  // open: bin, bout
  assign XOR_out = X ^ Y;  // XOR_Gate XOR, 32 bits wide
  assign NOR_out = ~(X | Y);  // NOR_Gate NOR, 32 bits wide
  Comparator #(.width(32), .mode("twosComplement")) comparator_1 (
    .a(X), .b(Y), .eq(Equal), .lt(comparator_1_lt[0]));  // open: gt
  Comparator #(.width(32), .mode("unsigned")) comparator_2 (.a(X), .b(Y), .lt(comparator_2_lt[0]));  // open: gt, eq
  Multiplexer #(.select(4), .width(32), .disabled("Z"), .enable("false")) multiplexer_1 (
    .in0(shifter_1_out), .in1(shifter_2_out), .in2(shifter_3_out), .in3(multiplier_1_out),
    .in4(divider_1_out), .in5(adder_1_out), .in6(subtractor_1_out), .in7(AND_out), .in8(OR_out),
    .in9(XOR_out), .in10(NOR_out), .in11({{31{1'b0}}, comparator_1_lt[0]}),
    .in12({{31{1'b0}}, comparator_2_lt[0]}), .in13({32{1'b0}}), .in14({32{1'b0}}), .in15({32{1'b0}}),
    .out(Result), .sel(AluOP));
  Multiplexer #(.select(4), .width(32), .disabled("Z"), .enable("false")) multiplexer_2 (
    .in0({32{1'b0}}), .in1({32{1'b0}}), .in2({32{1'b0}}), .in3(multiplier_1_cout), .in4(divider_1_rem),
    .in5({32{1'b0}}), .in6({32{1'b0}}), .in7({32{1'b0}}), .in8({32{1'b0}}), .in9({32{1'b0}}),
    .in10({32{1'b0}}), .in11({32{1'b0}}), .in12({32{1'b0}}), .in13({32{1'b0}}), .in14({32{1'b0}}),
    .in15({32{1'b0}}), .out(Result_2), .sel(AluOP));
  Multiplexer #(.select(4), .width(1), .disabled("Z"), .enable("false")) multiplexer_3 (
    .in0(1'b0), .in1(1'b0), .in2(1'b0), .in3(1'b0), .in4(1'b0), .in5(1'b0), .in6(1'b0), .in7(1'b0),
    .in8(1'b0), .in9(1'b0), .in10(1'b0), .in11(comparator_1_lt[0]), .in12(comparator_2_lt[0]), .in13(1'b0),
    .in14(1'b0), .in15(1'b0), .out(out_6), .sel(AluOP));
  not not_1 (out_4, out_6);

  // Other names for the same wires on the sheet: Result2[31:0] = Result_2; S[3:0] = AluOP; tunnel = out_6;
  //   tunnel_t = out_4

  // Notes on the sheet:
  //   不要改变此引脚区域内容，也不要改变ALU封装形式
  //   输入引脚
  //   输出引脚
endmodule

module Regifile (
  input  [31:0] Din,
  input  Clk,
  input  WE,
  input  [4:0] R1_num,
  input  [4:0] W_num,
  input  [4:0] R2_num,
  output [31:0] R1,
  output [31:0] R2
);

  // RegisterFile registerfile_1: pin names not known; wires that end beside it: Din, Clk, WE, W_num, R1_num, R2_num, R1, R2
endmodule

module \理想流水线  (
  output RegWrite,
  output MemWrite,
  output [31:0] IF_PC,
  output [31:0] ID_PC,
  output [31:0] EX_PC,
  output [31:0] M_PC,
  output [31:0] WB_PC,
  output [31:0] RDin,
  output [31:0] MDin,
  output [31:0] LedData
);

  wire and_1_out, and_2_out, and_4_out, CLK, clock_1_out, clock_2_out, comparator_1_eq, comparator_1_lt,
       comparator_2_eq, comparator_3_eq, d_ff_1_q, ecall, Go, halt, IR1, IR2, IR3, nand_1_out, not_1_out,
       not_2_out, or_1_out, RST, SType, W1, W2, W3, \单周期硬布线控制器_1_alu_src , \单周期硬布线控制器_1_beq ,
       \单周期硬布线控制器_1_bltu , \单周期硬布线控制器_1_bne , \单周期硬布线控制器_1_ecall , \单周期硬布线控制器_1_jal , \单周期硬布线控制器_1_jalr ,
       \单周期硬布线控制器_1_lb , \单周期硬布线控制器_1_lui , \单周期硬布线控制器_1_memtoreg , \单周期硬布线控制器_1_memwrite ,
       \单周期硬布线控制器_1_regwrite , \流水线通用组件_1_enable_2 , \流水线通用组件_2_alusrcb_2 , \流水线通用组件_2_beq_2 ,
       \流水线通用组件_2_bltu_2 , \流水线通用组件_2_bne_2 , \流水线通用组件_2_ecall_2 , \流水线通用组件_2_enable_2 , \流水线通用组件_2_jal_2 ,
       \流水线通用组件_2_jalr_2 , \流水线通用组件_2_lb_2 , \流水线通用组件_2_lui_2 , \流水线通用组件_2_memtoreg_2 ,
       \流水线通用组件_2_memwrite_2 , \流水线通用组件_2_regwrite_2 , \流水线通用组件_2_stype_2 , \流水线通用组件_3_alusrcb_2 ,
       \流水线通用组件_3_beq_2 , \流水线通用组件_3_bltu_2 , \流水线通用组件_3_bne_2 , \流水线通用组件_3_ecall_2 , \流水线通用组件_3_enable_2 ,
       \流水线通用组件_3_jal_2 , \流水线通用组件_3_jalr_2 , \流水线通用组件_3_lb_2 , \流水线通用组件_3_lui_2 , \流水线通用组件_3_memtoreg_2 ,
       \流水线通用组件_3_regwrite_2 , \流水线通用组件_3_stype_2 , \流水线通用组件_4_jal_2 , \流水线通用组件_4_jalr_2 , \流水线通用组件_4_lb_2 ,
       \流水线通用组件_4_lui_2 , \流水线通用组件_4_memtoreg_2 ;
  wire [3:0] \单周期硬布线控制器_1_alu_op , \流水线通用组件_2_aluop_2 , \流水线通用组件_3_aluop_2 ;
  wire [4:0] multiplexer_2_out, multiplexer_3_out;
  wire [7:0] multiplexer_5_out;
  wire [11:0] multiplexer_1_out;
  wire [12:0] CNT_num;
  wire [15:0] \LoadUse次数 , \总周期数 , \插入气泡数 , \无条件分支数 , \条件分支成功数 ;
  wire [31:0] adder_1_out, adder_2_out, adder_3_out, alu_1_result, and_3_out, bit_extender_1_out,
       bit_extender_2_out, bit_extender_3_out, bit_extender_4_out, EX_IR, ID_IR, IF_IR, MEM_IR,
       multiplexer_4_out, multiplexer_6_out, multiplexer_7_out, multiplexer_8_out, PC, ram_1_data,
       regifile_1_r1, regifile_1_r2, RegR1, RegR2, shifter_1_out, shifter_2_out, WB_IR, \流水线通用组件_1_pc_4_2 ,
       \流水线通用组件_2_bxxpc_2 , \流水线通用组件_2_imm12ext_2 , \流水线通用组件_2_jalpc_2 , \流水线通用组件_2_pc_4_2 ,
       \流水线通用组件_2_r1_2 , \流水线通用组件_2_r2_2 , \流水线通用组件_3_aluresult_2 , \流水线通用组件_3_bxxpc_2 ,
       \流水线通用组件_3_imm12ext_2 , \流水线通用组件_3_jalpc_2 , \流水线通用组件_3_pc_4_2 , \流水线通用组件_3_r1_2 ,
       \流水线通用组件_4_aluresult_2 , \流水线通用组件_4_memresult_2 , \流水线通用组件_4_pc_4_2 ;

  Button \u_总复位  (.out(RST));
  Button _1 (.out(IR1));
  Button _2 (.out(IR2));
  Button _3 (.out(IR3));
  // Probe on \总周期数 
  // Probe on \总周期数 
  Button \u_继续运行  (.out(Go));
  LED #(.active("true")) led_1 (.in(W1));
  LED #(.active("true")) led_2 (.in(W2));
  LED #(.active("true")) led_3 (.in(W3));
  Hex_Digit_Display hex_digit_display_1 (.value(LedData[31:28]));  // open: dp
  // Probe on IF_PC[19:0]
  // RiscV_Probe riscv_probe_1: pin names not known; wires that end beside it: IF_IR
  Hex_Digit_Display hex_digit_display_2 (.value(LedData[23:20]));  // open: dp
  Hex_Digit_Display hex_digit_display_3 (.value(LedData[27:24]));  // open: dp
  // Probe on ID_PC[19:0]
  // RiscV_Probe riscv_probe_2: pin names not known; wires that end beside it: ID_IR
  Hex_Digit_Display hex_digit_display_4 (.value(LedData[19:16]));  // open: dp
  Hex_Digit_Display hex_digit_display_5 (.value(LedData[15:12]));  // open: dp
  Register #(.width(32), .trigger("rising"), .Select("low")) u_PC (
    .D(adder_1_out), .en(not_1_out), .Q(IF_PC), .clk(CLK), .clr(RST));
  not not_1 (not_1_out, halt);
  Hex_Digit_Display hex_digit_display_6 (.value(LedData[7:4]));  // open: dp
  Hex_Digit_Display hex_digit_display_7 (.value(LedData[11:8]));  // open: dp
  Clock #(.highDuration(1), .lowDuration(1)) clock_1 (.out(clock_1_out));
  // Probe on EX_PC[19:0]
  // RiscV_Probe riscv_probe_3: pin names not known; wires that end beside it: clock_1_out, EX_IR, CLK
  Hex_Digit_Display hex_digit_display_8 (.value(LedData[3:0]));  // open: dp
  // Probe on \总周期数 
  // Probe on M_PC[19:0]
  // RiscV_Probe riscv_probe_4: pin names not known; wires that end beside it: MEM_IR
  ROM #(.addrWidth(10), .dataWidth(32), .Select("high")) rom_1 (.addr(IF_PC[11:2]), .data(IF_IR));
  Adder #(.width(32)) adder_1 (.a(IF_PC), .b(32'h4), .out(adder_1_out));  // open: cin, cout
  // Probe on \总周期数 
  // Probe on \无条件分支数 
  // Probe on \条件分支成功数 
  // Probe on \插入气泡数 
  // Probe on \LoadUse次数 
  // Probe on IF_PC[11:0]
  // Probe on WB_PC[19:0]
  // RiscV_Probe riscv_probe_5: pin names not known; wires that end beside it: WB_IR
  \流水线通用组件  \u_流水线通用组件_1  (
    .CLK(CLK), .Clear(1'b0), .PC(IF_PC), .IR(IF_IR), .PC_4(adder_1_out), .PC_2(ID_PC), .IR_2(ID_IR),
    .PC_4_2(\流水线通用组件_1_pc_4_2 ), .Enable(1'b1), .Enable_2(\流水线通用组件_1_enable_2 ));  // open: JALR, R1, JAL, R2, BEQ, BNE, AluResult, MemToReg, MemResult, MemWrite, AluOP, AluSrcB, RegWrite, SType, LUI, LB, BLTU, ECALL, JALR_2, R1_2, JAL_2, R2_2, BEQ_2, BNE_2, AluResult_2, MemToReg_2, MemResult_2, MemWrite_2, AluOP_2, AluSrcB_2, RegWrite_2, SType_2, LUI_2, LB_2, BLTU_2, ECALL_2, imm12ext, imm12ext_2, BXXpc, BXXpc_2, JALpc, JALpc_2, Stall, FwdR1, FwdR1_2, FwdR2, FwdR2_2
  // Probe on EX_PC[11:0]
  // Probe on ID_PC[11:0]
  // Probe on M_PC[11:0]
  D_Flip_Flop #(.trigger("high"), .Pre_Clr_Positions("LEGACY"), .NegatePresetClear("false"), .enable("true"), .NewFFLayout("false")) d_ff_1 (.Q(d_ff_1_q));  // open: clk, D, Qn, preset, en, reset
  // Probe on 13'hc
  // Probe on WB_PC[11:0]
  Comparator #(.width(13), .mode("twosComplement")) comparator_1 (
    .a(CNT_num), .b(13'hc), .eq(comparator_1_eq), .lt(comparator_1_lt));  // open: gt
  Clock #(.highDuration(1), .lowDuration(1)) clock_2 (.out(clock_2_out));
  \单周期硬布线控制器  \u_单周期硬布线控制器_1  (
    .Funct({ID_IR[30], ID_IR[25], ID_IR[14:12]}), .OP(ID_IR[6:2]), .ALU_OP(\单周期硬布线控制器_1_alu_op ),
    .MemToReg(\单周期硬布线控制器_1_memtoreg ), .MemWrite(\单周期硬布线控制器_1_memwrite ), .ALU_SRC(\单周期硬布线控制器_1_alu_src ),
    .RegWrite(\单周期硬布线控制器_1_regwrite ), .ecall(\单周期硬布线控制器_1_ecall ), .S_type(SType),
    .Jalr(\单周期硬布线控制器_1_jalr ), .Beq(\单周期硬布线控制器_1_beq ), .JAL(\单周期硬布线控制器_1_jal ), .Bne(\单周期硬布线控制器_1_bne ),
    .BLTU(\单周期硬布线控制器_1_bltu ), .LB(\单周期硬布线控制器_1_lb ), .LUI(\单周期硬布线控制器_1_lui ));  // open: NotNop
  Multiplexer #(.select(1), .width(12), .disabled("Z"), .enable("false")) multiplexer_1 (
    .in0(ID_IR[31:20]), .in1({ID_IR[31:25], ID_IR[11:7]}), .out(multiplexer_1_out), .sel(SType));
  nand nand_1 (nand_1_out, d_ff_1_q, comparator_1_eq);
  Counter #(.width(13), .max('h1fff), .ongoal("stay"), .trigger("rising"), .behavior("old")) counter_1 (
    .count(comparator_1_lt), .Q(CNT_num), .clk(clock_2_out));  // open: load, D, carry, clr, preset
  assign bit_extender_1_out = {{20{multiplexer_1_out[11]}}, multiplexer_1_out};  // Bit_Extender bit_extender_1
  assign bit_extender_2_out = {{20{ID_IR[31]}}, {ID_IR[31], ID_IR[7], ID_IR[30:25], ID_IR[11:8]}};  // Bit_Extender bit_extender_2
  assign bit_extender_3_out = {{12{ID_IR[31]}}, {ID_IR[31], ID_IR[19:12], ID_IR[20], ID_IR[30:21]}};  // Bit_Extender bit_extender_3
  assign CLK = nand_1_out ? clock_2_out : 1'bz;  // Controlled_Buffer controlled_buffer_1
  Multiplexer #(.select(1), .width(5), .disabled("Z"), .enable("false")) multiplexer_2 (
    .in0(ID_IR[24:20]), .in1(5'b10001), .out(multiplexer_2_out), .sel(\单周期硬布线控制器_1_ecall ));
  Shifter #(.width(32), .shift("ll")) shifter_1 (.in(bit_extender_2_out), .\dist (5'b00001), .out(shifter_1_out));
  Shifter #(.width(32), .shift("ll")) shifter_2 (.in(bit_extender_3_out), .\dist (5'b00001), .out(shifter_2_out));
  Pull_Resistor #(.pull(1)) pull_resistor_1 (.node(CLK));
  Multiplexer #(.select(1), .width(5), .disabled("Z"), .enable("false")) multiplexer_3 (
    .in0(ID_IR[19:15]), .in1(5'b01010), .out(multiplexer_3_out), .sel(\单周期硬布线控制器_1_ecall ));
  Adder #(.width(32)) adder_2 (.a(PC), .b(shifter_1_out), .out(adder_2_out));  // open: cin, cout
  Adder #(.width(32)) adder_3 (.a(PC), .b(shifter_2_out), .out(adder_3_out));  // open: cin, cout
  Regifile regifile_1 (
    .Din(RDin), .Clk(CLK), .R1(regifile_1_r1), .R2(regifile_1_r2), .WE(RegWrite), .W_num(WB_IR[11:7]),
    .R1_num(multiplexer_3_out), .R2_num(multiplexer_2_out));
  \流水线通用组件  \u_流水线通用组件_2  (
    .CLK(CLK), .Clear(1'b0), .PC(ID_PC), .JALR(\单周期硬布线控制器_1_jalr ), .R1(regifile_1_r1),
    .JAL(\单周期硬布线控制器_1_jal ), .IR(ID_IR), .R2(regifile_1_r2), .BEQ(\单周期硬布线控制器_1_beq ),
    .PC_4(\流水线通用组件_1_pc_4_2 ), .BNE(\单周期硬布线控制器_1_bne ), .MemToReg(\单周期硬布线控制器_1_memtoreg ),
    .MemWrite(\单周期硬布线控制器_1_memwrite ), .AluOP(\单周期硬布线控制器_1_alu_op ), .AluSrcB(\单周期硬布线控制器_1_alu_src ),
    .RegWrite(\单周期硬布线控制器_1_regwrite ), .SType(SType), .LUI(\单周期硬布线控制器_1_lui ), .LB(\单周期硬布线控制器_1_lb ),
    .BLTU(\单周期硬布线控制器_1_bltu ), .ECALL(\单周期硬布线控制器_1_ecall ), .PC_2(EX_PC), .JALR_2(\流水线通用组件_2_jalr_2 ),
    .R1_2(\流水线通用组件_2_r1_2 ), .JAL_2(\流水线通用组件_2_jal_2 ), .IR_2(EX_IR), .R2_2(\流水线通用组件_2_r2_2 ),
    .BEQ_2(\流水线通用组件_2_beq_2 ), .PC_4_2(\流水线通用组件_2_pc_4_2 ), .BNE_2(\流水线通用组件_2_bne_2 ),
    .MemToReg_2(\流水线通用组件_2_memtoreg_2 ), .MemWrite_2(\流水线通用组件_2_memwrite_2 ), .AluOP_2(\流水线通用组件_2_aluop_2 ),
    .AluSrcB_2(\流水线通用组件_2_alusrcb_2 ), .RegWrite_2(\流水线通用组件_2_regwrite_2 ), .SType_2(\流水线通用组件_2_stype_2 ),
    .LUI_2(\流水线通用组件_2_lui_2 ), .LB_2(\流水线通用组件_2_lb_2 ), .BLTU_2(\流水线通用组件_2_bltu_2 ),
    .ECALL_2(\流水线通用组件_2_ecall_2 ), .imm12ext(bit_extender_1_out), .imm12ext_2(\流水线通用组件_2_imm12ext_2 ),
    .BXXpc(adder_2_out), .BXXpc_2(\流水线通用组件_2_bxxpc_2 ), .JALpc(adder_3_out), .JALpc_2(\流水线通用组件_2_jalpc_2 ),
    .Enable(\流水线通用组件_1_enable_2 ), .Enable_2(\流水线通用组件_2_enable_2 ));  // open: AluResult, MemResult, AluResult_2, MemResult_2, Stall, FwdR1, FwdR1_2, FwdR2, FwdR2_2
  Multiplexer #(.select(1), .width(32), .disabled("Z"), .enable("false")) multiplexer_4 (
    .in0(\流水线通用组件_2_r2_2 ), .in1(\流水线通用组件_2_imm12ext_2 ), .out(multiplexer_4_out), .sel(\流水线通用组件_2_alusrcb_2 ));
  ALU alu_1 (
    .X(\流水线通用组件_2_r1_2 ), .Y(multiplexer_4_out), .AluOP(\流水线通用组件_2_aluop_2 ), .Result(alu_1_result));  // open: Equal, Result_2, out_4, out_6
  \流水线通用组件  \u_流水线通用组件_3  (
    .CLK(CLK), .Clear(1'b0), .PC(EX_PC), .JALR(\流水线通用组件_2_jalr_2 ), .R1(\流水线通用组件_2_r1_2 ),
    .JAL(\流水线通用组件_2_jal_2 ), .IR(EX_IR), .R2(\流水线通用组件_2_r2_2 ), .BEQ(\流水线通用组件_2_beq_2 ),
    .PC_4(\流水线通用组件_2_pc_4_2 ), .BNE(\流水线通用组件_2_bne_2 ), .AluResult(alu_1_result),
    .MemToReg(\流水线通用组件_2_memtoreg_2 ), .MemWrite(\流水线通用组件_2_memwrite_2 ), .AluOP(\流水线通用组件_2_aluop_2 ),
    .AluSrcB(\流水线通用组件_2_alusrcb_2 ), .RegWrite(\流水线通用组件_2_regwrite_2 ), .SType(\流水线通用组件_2_stype_2 ),
    .LUI(\流水线通用组件_2_lui_2 ), .LB(\流水线通用组件_2_lb_2 ), .BLTU(\流水线通用组件_2_bltu_2 ), .ECALL(\流水线通用组件_2_ecall_2 ),
    .PC_2(M_PC), .JALR_2(\流水线通用组件_3_jalr_2 ), .R1_2(\流水线通用组件_3_r1_2 ), .JAL_2(\流水线通用组件_3_jal_2 ),
    .IR_2(MEM_IR), .R2_2(MDin), .BEQ_2(\流水线通用组件_3_beq_2 ), .PC_4_2(\流水线通用组件_3_pc_4_2 ),
    .BNE_2(\流水线通用组件_3_bne_2 ), .AluResult_2(\流水线通用组件_3_aluresult_2 ), .MemToReg_2(\流水线通用组件_3_memtoreg_2 ),
    .MemWrite_2(MemWrite), .AluOP_2(\流水线通用组件_3_aluop_2 ), .AluSrcB_2(\流水线通用组件_3_alusrcb_2 ),
    .RegWrite_2(\流水线通用组件_3_regwrite_2 ), .SType_2(\流水线通用组件_3_stype_2 ), .LUI_2(\流水线通用组件_3_lui_2 ),
    .LB_2(\流水线通用组件_3_lb_2 ), .BLTU_2(\流水线通用组件_3_bltu_2 ), .ECALL_2(\流水线通用组件_3_ecall_2 ),
    .imm12ext(\流水线通用组件_2_imm12ext_2 ), .imm12ext_2(\流水线通用组件_3_imm12ext_2 ), .BXXpc(\流水线通用组件_2_bxxpc_2 ),
    .BXXpc_2(\流水线通用组件_3_bxxpc_2 ), .JALpc(\流水线通用组件_2_jalpc_2 ), .JALpc_2(\流水线通用组件_3_jalpc_2 ),
    .Enable(\流水线通用组件_2_enable_2 ), .Enable_2(\流水线通用组件_3_enable_2 ));  // open: MemResult, MemResult_2, Stall, FwdR1, FwdR1_2, FwdR2, FwdR2_2
  and and_1 (and_1_out, CLK, ~halt);  // AND_Gate
  Counter #(.width(16), .max('hffff), .ongoal("stay"), .trigger("rising"), .behavior("old")) counter_2 (
    .Q(\总周期数 ), .clk(and_1_out));  // open: load, D, count, carry, clr, preset
  RAM #(.addrWidth(10), .dataWidth(32), .bus("separate"), .Select("high")) ram_1 (
    .addr(\流水线通用组件_3_aluresult_2 [11:2]), .din(MDin), .data(ram_1_data), .str(MemWrite), .clk(CLK));  // open: sel, ld, clr
  \流水线通用组件  \u_流水线通用组件_4  (
    .CLK(CLK), .Clear(1'b0), .PC(M_PC), .JALR(\流水线通用组件_3_jalr_2 ), .R1(\流水线通用组件_3_r1_2 ),
    .JAL(\流水线通用组件_3_jal_2 ), .IR(MEM_IR), .R2(MDin), .BEQ(\流水线通用组件_3_beq_2 ), .PC_4(\流水线通用组件_3_pc_4_2 ),
    .BNE(\流水线通用组件_3_bne_2 ), .AluResult(\流水线通用组件_3_aluresult_2 ), .MemToReg(\流水线通用组件_3_memtoreg_2 ),
    .MemResult(ram_1_data), .MemWrite(MemWrite), .AluOP(\流水线通用组件_3_aluop_2 ),
    .AluSrcB(\流水线通用组件_3_alusrcb_2 ), .RegWrite(\流水线通用组件_3_regwrite_2 ), .SType(\流水线通用组件_3_stype_2 ),
    .LUI(\流水线通用组件_3_lui_2 ), .LB(\流水线通用组件_3_lb_2 ), .BLTU(\流水线通用组件_3_bltu_2 ), .ECALL(\流水线通用组件_3_ecall_2 ),
    .PC_2(WB_PC), .JALR_2(\流水线通用组件_4_jalr_2 ), .R1_2(RegR1), .JAL_2(\流水线通用组件_4_jal_2 ), .IR_2(WB_IR),
    .R2_2(RegR2), .PC_4_2(\流水线通用组件_4_pc_4_2 ), .AluResult_2(\流水线通用组件_4_aluresult_2 ),
    .MemToReg_2(\流水线通用组件_4_memtoreg_2 ), .MemResult_2(\流水线通用组件_4_memresult_2 ), .RegWrite_2(RegWrite),
    .LUI_2(\流水线通用组件_4_lui_2 ), .LB_2(\流水线通用组件_4_lb_2 ), .ECALL_2(ecall), .imm12ext(\流水线通用组件_3_imm12ext_2 ),
    .BXXpc(\流水线通用组件_3_bxxpc_2 ), .JALpc(\流水线通用组件_3_jalpc_2 ), .Enable(\流水线通用组件_3_enable_2 ));  // open: BEQ_2, BNE_2, MemWrite_2, AluOP_2, AluSrcB_2, SType_2, BLTU_2, imm12ext_2, BXXpc_2, JALpc_2, Enable_2, Stall, FwdR1, FwdR1_2, FwdR2, FwdR2_2
  Comparator #(.width(32), .mode("twosComplement")) comparator_2 (
    .a(RegR2), .b(32'h22), .eq(comparator_2_eq));  // open: gt, lt
  and and_2 (and_2_out, ecall, comparator_2_eq);
  or or_1 (or_1_out, \流水线通用组件_4_jalr_2 , \流水线通用组件_4_jal_2 );
  Multiplexer #(.select(2), .width(8), .disabled("Z"), .enable("false")) multiplexer_5 (
    .in0(\流水线通用组件_4_memresult_2 [7:0]), .in1(\流水线通用组件_4_memresult_2 [15:8]),
    .in2(\流水线通用组件_4_memresult_2 [23:16]), .in3(\流水线通用组件_4_memresult_2 [31:24]), .out(multiplexer_5_out),
    .sel(\流水线通用组件_4_aluresult_2 [1:0]));
  assign and_3_out = 32'hfffff000 & WB_IR;  // AND_Gate and_3, 32 bits wide
  Register #(.width(32), .trigger("rising"), .Select("low")) register_1 (
    .D(RegR1), .en(and_2_out), .Q(LedData), .clk(CLK));  // open: clr
  assign bit_extender_4_out = {{24{multiplexer_5_out[7]}}, multiplexer_5_out};  // Bit_Extender bit_extender_4
  Multiplexer #(.select(1), .width(32), .disabled("Z"), .enable("false")) multiplexer_6 (
    .in0(\流水线通用组件_4_memresult_2 ), .in1(bit_extender_4_out), .out(multiplexer_6_out), .sel(\流水线通用组件_4_lb_2 ));
  Multiplexer #(.select(1), .width(32), .disabled("Z"), .enable("false")) multiplexer_7 (
    .in0(\流水线通用组件_4_aluresult_2 ), .in1(multiplexer_6_out), .out(multiplexer_7_out),
    .sel(\流水线通用组件_4_memtoreg_2 ));
  Comparator #(.width(32), .mode("twosComplement")) comparator_3 (
    .a(RegR2), .b(32'ha), .eq(comparator_3_eq));  // open: gt, lt
  Multiplexer #(.select(1), .width(32), .disabled("Z"), .enable("false")) multiplexer_8 (
    .in0(multiplexer_7_out), .in1(and_3_out), .out(multiplexer_8_out), .sel(\流水线通用组件_4_lui_2 ));
  Multiplexer #(.select(1), .width(32), .disabled("Z"), .enable("false")) multiplexer_9 (
    .in0(multiplexer_8_out), .in1(\流水线通用组件_4_pc_4_2 ), .out(RDin), .sel(or_1_out));
  and and_4 (and_4_out, ecall, comparator_3_eq);
  not not_2 (not_2_out, halt);
  Register #(.width(1), .trigger("rising"), .Select("low")) register_2 (
    .D(and_4_out), .en(not_2_out), .Q(halt), .clk(CLK));  // open: clr

  // Other names for the same wires on the sheet: MEM_PC[31:0] = M_PC; WriteBack_Rd[4:0] = WB_IR[11:7];
  //   WriteBack_We = RegWrite

  // Notes on the sheet:
  //   中断源
  //   时空图监测，可删除
  //   中断等待指示
  //   数码管输出
  //   contents of rom_1 (hex, n*v repeats v):
  //   413 493 913 993 46413 14e493 296913 39e993 842023 942223 1242423 1342623 a00893 493 913 993 73
  //   控制位
  //   流水调试日志用
  //   暂停节拍，不能为0
  //   RS1
  //   RS2
  //   imm12
  //   戳工具置1进入计数暂停模式，ctrl+k时钟自动运行到对应节拍暂停
  //   ctrl+k关闭时钟连续运行，将控制位置零，进入单步调试模式调试
  //   用这个时钟源需要去掉电路中的其他时钟源
  //   a7
  //   可计数暂停的时钟源
  //   a0
  //   为方便自动评测，需要输出流水线各段保存的PC值，注意是PC不是PC+4，另外ID段寄存器写入信息，Mem段内存写入信息也要输出
endmodule

module \气泡流水线  (
  output RegWrite,
  output MemWrite,
  output [31:0] IF_PC,
  output [31:0] ID_PC,
  output [31:0] EX_PC,
  output [31:0] M_PC,
  output [31:0] WB_PC,
  output [31:0] RDin,
  output [31:0] MDin,
  output [31:0] LedData
);

  wire alu_1_equal, alu_1_out_6, and_1_out, and_2_out, and_4_out, and_5_out, and_6_out, Bubble, CLK,
       clock_1_out, clock_2_out, comparator_1_eq, comparator_1_lt, comparator_3_eq, comparator_4_eq,
       d_ff_1_q, ecall, ExRegWrite, Go, halt, IR1, IR2, IR3, MemRegWrite, nand_1_out, not_1_out, not_2_out,
       not_3_out, or_1_out, or_2_out, or_3_out, RST, Stall, SType, W1, W2, W3, \单周期硬布线控制器_1_alu_src ,
       \单周期硬布线控制器_1_beq , \单周期硬布线控制器_1_bltu , \单周期硬布线控制器_1_bne , \单周期硬布线控制器_1_ecall , \单周期硬布线控制器_1_jal ,
       \单周期硬布线控制器_1_jalr , \单周期硬布线控制器_1_lb , \单周期硬布线控制器_1_lui , \单周期硬布线控制器_1_memtoreg ,
       \单周期硬布线控制器_1_memwrite , \单周期硬布线控制器_1_regwrite , \流水线通用组件_1_enable_2 , \流水线通用组件_2_alusrcb_2 ,
       \流水线通用组件_2_beq_2 , \流水线通用组件_2_bltu_2 , \流水线通用组件_2_bne_2 , \流水线通用组件_2_ecall_2 , \流水线通用组件_2_enable_2 ,
       \流水线通用组件_2_jal_2 , \流水线通用组件_2_jalr_2 , \流水线通用组件_2_lb_2 , \流水线通用组件_2_lui_2 , \流水线通用组件_2_memtoreg_2 ,
       \流水线通用组件_2_memwrite_2 , \流水线通用组件_2_stype_2 , \流水线通用组件_3_alusrcb_2 , \流水线通用组件_3_beq_2 ,
       \流水线通用组件_3_bltu_2 , \流水线通用组件_3_bne_2 , \流水线通用组件_3_ecall_2 , \流水线通用组件_3_enable_2 , \流水线通用组件_3_jal_2 ,
       \流水线通用组件_3_jalr_2 , \流水线通用组件_3_lb_2 , \流水线通用组件_3_lui_2 , \流水线通用组件_3_memtoreg_2 , \流水线通用组件_3_stype_2 ,
       \流水线通用组件_4_jal_2 , \流水线通用组件_4_jalr_2 , \流水线通用组件_4_lb_2 , \流水线通用组件_4_lui_2 , \流水线通用组件_4_memtoreg_2 ;
  wire [2:0] NextPCSelector;
  wire [3:0] \单周期硬布线控制器_1_alu_op , \流水线通用组件_2_aluop_2 , \流水线通用组件_3_aluop_2 ;
  wire [4:0] multiplexer_3_out, multiplexer_4_out;
  wire [7:0] multiplexer_7_out;
  wire [11:0] multiplexer_2_out;
  wire [12:0] CNT_num;
  wire [15:0] \LoadUse次数 , \总周期数 , \插入气泡数 , \无条件分支数 , \条件分支成功数 ;
  wire [31:0] adder_1_out, adder_2_out, adder_3_out, alu_1_result, and_3_out, and_7_out, bit_extender_1_out,
       bit_extender_2_out, bit_extender_3_out, bit_extender_4_out, EX_IR, ID_IR, IF_IR, MEM_IR,
       multiplexer_1_out, multiplexer_5_out, multiplexer_6_out, multiplexer_8_out, multiplexer_9_out,
       multiplexer_10_out, ram_1_data, regifile_1_r1, regifile_1_r2, RegR1, RegR2, shifter_1_out,
       shifter_2_out, WB_IR, \流水线通用组件_1_pc_4_2 , \流水线通用组件_2_bxxpc_2 , \流水线通用组件_2_imm12ext_2 ,
       \流水线通用组件_2_jalpc_2 , \流水线通用组件_2_pc_4_2 , \流水线通用组件_2_r1_2 , \流水线通用组件_2_r2_2 , \流水线通用组件_3_aluresult_2 ,
       \流水线通用组件_3_bxxpc_2 , \流水线通用组件_3_imm12ext_2 , \流水线通用组件_3_jalpc_2 , \流水线通用组件_3_pc_4_2 ,
       \流水线通用组件_3_r1_2 , \流水线通用组件_4_aluresult_2 , \流水线通用组件_4_memresult_2 , \流水线通用组件_4_pc_4_2 ;

  Button \u_总复位  (.out(RST));
  Button _1 (.out(IR1));
  Button _2 (.out(IR2));
  Button _3 (.out(IR3));
  // Probe on \总周期数 
  // Probe on \总周期数 
  Button \u_继续运行  (.out(Go));
  LED #(.active("true")) led_1 (.in(W1));
  LED #(.active("true")) led_2 (.in(W2));
  LED #(.active("true")) led_3 (.in(W3));
  Hex_Digit_Display hex_digit_display_1 (.value(LedData[31:28]));  // open: dp
  // Probe on IF_PC[19:0]
  // RiscV_Probe riscv_probe_1: pin names not known; wires that end beside it: IF_IR
  Hex_Digit_Display hex_digit_display_2 (.value(LedData[23:20]));  // open: dp
  Hex_Digit_Display hex_digit_display_3 (.value(LedData[27:24]));  // open: dp
  // Probe on ID_PC[19:0]
  // RiscV_Probe riscv_probe_2: pin names not known; wires that end beside it: ID_IR
  not not_1 (not_1_out, or_1_out);
  or or_1 (or_1_out, halt, Stall);
  Hex_Digit_Display hex_digit_display_4 (.value(LedData[15:12]));  // open: dp
  Hex_Digit_Display hex_digit_display_5 (.value(LedData[19:16]));  // open: dp
  Register #(.width(32), .trigger("rising"), .Select("low")) PC (
    .D(multiplexer_1_out), .en(not_1_out), .Q(IF_PC), .clk(CLK), .clr(RST));
  Hex_Digit_Display hex_digit_display_6 (.value(LedData[7:4]));  // open: dp
  Hex_Digit_Display hex_digit_display_7 (.value(LedData[11:8]));  // open: dp
  Clock #(.highDuration(1), .lowDuration(1)) clock_1 (.out(clock_1_out));
  // Probe on EX_PC[19:0]
  // RiscV_Probe riscv_probe_3: pin names not known; wires that end beside it: clock_1_out, EX_IR, CLK
  Multiplexer #(.select(1), .width(32), .disabled("Z"), .enable("false")) multiplexer_1 (
    .in0(adder_1_out), .in1(multiplexer_6_out), .out(multiplexer_1_out), .sel(Bubble));
  Hex_Digit_Display hex_digit_display_8 (.value(LedData[3:0]));  // open: dp
  ROM #(.addrWidth(10), .dataWidth(32), .Select("high")) rom_1 (.addr(IF_PC[11:2]), .data(IF_IR));
  Adder #(.width(32)) adder_1 (.a(IF_PC), .b(32'h4), .out(adder_1_out));  // open: cin, cout
  // Probe on \总周期数 
  // Probe on M_PC[19:0]
  // RiscV_Probe riscv_probe_4: pin names not known; wires that end beside it: MEM_IR
  // Probe on \总周期数 
  // Probe on \无条件分支数 
  // Probe on \条件分支成功数 
  // Probe on \插入气泡数 
  // Probe on \LoadUse次数 
  \流水线通用组件  \u_流水线通用组件_1  (
    .CLK(CLK), .Clear(Bubble), .PC(IF_PC), .IR(IF_IR), .PC_4(adder_1_out), .PC_2(ID_PC), .IR_2(ID_IR),
    .PC_4_2(\流水线通用组件_1_pc_4_2 ), .Enable(1'b1), .Enable_2(\流水线通用组件_1_enable_2 ), .Stall(Stall));  // open: JALR, R1, JAL, R2, BEQ, BNE, AluResult, MemToReg, MemResult, MemWrite, AluOP, AluSrcB, RegWrite, SType, LUI, LB, BLTU, ECALL, JALR_2, R1_2, JAL_2, R2_2, BEQ_2, BNE_2, AluResult_2, MemToReg_2, MemResult_2, MemWrite_2, AluOP_2, AluSrcB_2, RegWrite_2, SType_2, LUI_2, LB_2, BLTU_2, ECALL_2, imm12ext, imm12ext_2, BXXpc, BXXpc_2, JALpc, JALpc_2, FwdR1, FwdR1_2, FwdR2, FwdR2_2
  // Probe on IF_PC[11:0]
  // Probe on WB_PC[19:0]
  // RiscV_Probe riscv_probe_5: pin names not known; wires that end beside it: WB_IR
  // Probe on EX_PC[11:0]
  // Probe on ID_PC[11:0]
  // Probe on M_PC[11:0]
  D_Flip_Flop #(.trigger("high"), .Pre_Clr_Positions("LEGACY"), .NegatePresetClear("false"), .enable("true"), .NewFFLayout("false")) d_ff_1 (.Q(d_ff_1_q));  // open: clk, D, Qn, preset, en, reset
  // Probe on 13'h56
  Multiplexer #(.select(1), .width(12), .disabled("Z"), .enable("false")) multiplexer_2 (
    .in0(ID_IR[31:20]), .in1({ID_IR[31:25], ID_IR[11:7]}), .out(multiplexer_2_out), .sel(SType));
  // Probe on WB_PC[11:0]
  Comparator #(.width(13), .mode("twosComplement")) comparator_1 (
    .a(CNT_num), .b(13'h56), .eq(comparator_1_eq), .lt(comparator_1_lt));  // open: gt
  Clock #(.highDuration(1), .lowDuration(1)) clock_2 (.out(clock_2_out));
  \单周期硬布线控制器  \u_单周期硬布线控制器_1  (
    .Funct({ID_IR[30], ID_IR[25], ID_IR[14:12]}), .OP(ID_IR[6:2]), .ALU_OP(\单周期硬布线控制器_1_alu_op ),
    .MemToReg(\单周期硬布线控制器_1_memtoreg ), .MemWrite(\单周期硬布线控制器_1_memwrite ), .ALU_SRC(\单周期硬布线控制器_1_alu_src ),
    .RegWrite(\单周期硬布线控制器_1_regwrite ), .ecall(\单周期硬布线控制器_1_ecall ), .S_type(SType),
    .Jalr(\单周期硬布线控制器_1_jalr ), .Beq(\单周期硬布线控制器_1_beq ), .JAL(\单周期硬布线控制器_1_jal ), .Bne(\单周期硬布线控制器_1_bne ),
    .BLTU(\单周期硬布线控制器_1_bltu ), .LB(\单周期硬布线控制器_1_lb ), .LUI(\单周期硬布线控制器_1_lui ));  // open: NotNop
  assign bit_extender_1_out = {{20{multiplexer_2_out[11]}}, multiplexer_2_out};  // Bit_Extender bit_extender_1
  assign bit_extender_2_out = {{20{ID_IR[31]}}, {ID_IR[31], ID_IR[7], ID_IR[30:25], ID_IR[11:8]}};  // Bit_Extender bit_extender_2
  assign bit_extender_3_out = {{12{ID_IR[31]}}, {ID_IR[31], ID_IR[19:12], ID_IR[20], ID_IR[30:21]}};  // Bit_Extender bit_extender_3
  nand nand_1 (nand_1_out, d_ff_1_q, comparator_1_eq);
  Counter #(.width(13), .max('h1fff), .ongoal("stay"), .trigger("rising"), .behavior("old")) counter_1 (
    .count(comparator_1_lt), .Q(CNT_num), .clk(clock_2_out));  // open: load, D, carry, clr, preset
  Multiplexer #(.select(1), .width(5), .disabled("Z"), .enable("false")) multiplexer_3 (
    .in0(ID_IR[24:20]), .in1(5'b10001), .out(multiplexer_3_out), .sel(\单周期硬布线控制器_1_ecall ));
  Shifter #(.width(32), .shift("ll")) shifter_1 (.in(bit_extender_2_out), .\dist (5'b00001), .out(shifter_1_out));
  Shifter #(.width(32), .shift("ll")) shifter_2 (.in(bit_extender_3_out), .\dist (5'b00001), .out(shifter_2_out));
  assign CLK = nand_1_out ? clock_2_out : 1'bz;  // Controlled_Buffer controlled_buffer_1
  Multiplexer #(.select(1), .width(5), .disabled("Z"), .enable("false")) multiplexer_4 (
    .in0(ID_IR[19:15]), .in1(5'b01010), .out(multiplexer_4_out), .sel(\单周期硬布线控制器_1_ecall ));
  Adder #(.width(32)) adder_2 (.a(ID_PC), .b(shifter_1_out), .out(adder_2_out));  // open: cin, cout
  Adder #(.width(32)) adder_3 (.a(ID_PC), .b(shifter_2_out), .out(adder_3_out));  // open: cin, cout
  Pull_Resistor #(.pull(1)) pull_resistor_1 (.node(CLK));
  // 寄存器使用情况 寄存器使用情况_1: pin names not known; wires that end beside it: ID_IR[6:2], {ID_IR[30], ID_IR[25], ID_IR[14:12]}, multiplexer_4_out, multiplexer_3_out, ExRegWrite, EX_IR[11:7], MemRegWrite, MEM_IR[11:7], MEM_IR[11:7], MemRegWrite, Stall, MEM_IR[11:7], EX_IR[11:7]
  Regifile regifile_1 (
    .Din(RDin), .Clk(CLK), .R1(regifile_1_r1), .R2(regifile_1_r2), .WE(RegWrite), .W_num(WB_IR[11:7]),
    .R1_num(multiplexer_4_out), .R2_num(multiplexer_3_out));
  \流水线通用组件  \u_流水线通用组件_2  (
    .CLK(CLK), .Clear(or_2_out), .PC(ID_PC), .JALR(\单周期硬布线控制器_1_jalr ), .R1(regifile_1_r1),
    .JAL(\单周期硬布线控制器_1_jal ), .IR(ID_IR), .R2(regifile_1_r2), .BEQ(\单周期硬布线控制器_1_beq ),
    .PC_4(\流水线通用组件_1_pc_4_2 ), .BNE(\单周期硬布线控制器_1_bne ), .MemToReg(\单周期硬布线控制器_1_memtoreg ),
    .MemWrite(\单周期硬布线控制器_1_memwrite ), .AluOP(\单周期硬布线控制器_1_alu_op ), .AluSrcB(\单周期硬布线控制器_1_alu_src ),
    .RegWrite(\单周期硬布线控制器_1_regwrite ), .SType(SType), .LUI(\单周期硬布线控制器_1_lui ), .LB(\单周期硬布线控制器_1_lb ),
    .BLTU(\单周期硬布线控制器_1_bltu ), .ECALL(\单周期硬布线控制器_1_ecall ), .PC_2(EX_PC), .JALR_2(\流水线通用组件_2_jalr_2 ),
    .R1_2(\流水线通用组件_2_r1_2 ), .JAL_2(\流水线通用组件_2_jal_2 ), .IR_2(EX_IR), .R2_2(\流水线通用组件_2_r2_2 ),
    .BEQ_2(\流水线通用组件_2_beq_2 ), .PC_4_2(\流水线通用组件_2_pc_4_2 ), .BNE_2(\流水线通用组件_2_bne_2 ),
    .MemToReg_2(\流水线通用组件_2_memtoreg_2 ), .MemWrite_2(\流水线通用组件_2_memwrite_2 ), .AluOP_2(\流水线通用组件_2_aluop_2 ),
    .AluSrcB_2(\流水线通用组件_2_alusrcb_2 ), .RegWrite_2(ExRegWrite), .SType_2(\流水线通用组件_2_stype_2 ),
    .LUI_2(\流水线通用组件_2_lui_2 ), .LB_2(\流水线通用组件_2_lb_2 ), .BLTU_2(\流水线通用组件_2_bltu_2 ),
    .ECALL_2(\流水线通用组件_2_ecall_2 ), .imm12ext(bit_extender_1_out), .imm12ext_2(\流水线通用组件_2_imm12ext_2 ),
    .BXXpc(adder_2_out), .BXXpc_2(\流水线通用组件_2_bxxpc_2 ), .JALpc(adder_3_out), .JALpc_2(\流水线通用组件_2_jalpc_2 ),
    .Enable(\流水线通用组件_1_enable_2 ), .Enable_2(\流水线通用组件_2_enable_2 ), .Stall(1'b0));  // open: AluResult, MemResult, AluResult_2, MemResult_2, FwdR1, FwdR1_2, FwdR2, FwdR2_2
  or or_2 (or_2_out, Bubble, Stall);
  Multiplexer #(.select(1), .width(32), .disabled("Z"), .enable("false")) multiplexer_5 (
    .in0(\流水线通用组件_2_r2_2 ), .in1(\流水线通用组件_2_imm12ext_2 ), .out(multiplexer_5_out), .sel(\流水线通用组件_2_alusrcb_2 ));
  Multiplexer #(.select(3), .width(32), .disabled("Z"), .enable("false")) multiplexer_6 (
    .in0(\流水线通用组件_2_pc_4_2 ), .in1(and_3_out), .in2(\流水线通用组件_2_jalpc_2 ), .in3(\流水线通用组件_2_bxxpc_2 ),
    .in4(\流水线通用组件_2_bxxpc_2 ), .in5(\流水线通用组件_2_bxxpc_2 ), .out(multiplexer_6_out), .sel(NextPCSelector));  // open: in6, in7
  Priority_Encoder #(.select(3), .disabled("Z")) priority_encoder_1 (
    .in0(1'b1), .in1(\流水线通用组件_2_jalr_2 ), .in2(\流水线通用组件_2_jal_2 ), .in3(and_1_out), .in4(and_2_out),
    .in5(and_4_out), .out(NextPCSelector), .en_in(1'b1));  // open: in6, in7, gs, en_out
  and and_1 (and_1_out, \流水线通用组件_2_beq_2 , alu_1_equal);
  and and_2 (and_2_out, \流水线通用组件_2_bne_2 , ~alu_1_equal);  // AND_Gate
  assign and_3_out = alu_1_result & 32'hfffffffe;  // AND_Gate and_3, 32 bits wide
  Comparator #(.width(3), .mode("unsigned")) comparator_2 (
    .a(NextPCSelector), .b(3'b000), .gt(Bubble));  // open: eq, lt
  and and_4 (and_4_out, \流水线通用组件_2_bltu_2 , alu_1_out_6);
  ALU alu_1 (
    .X(\流水线通用组件_2_r1_2 ), .Y(multiplexer_5_out), .AluOP(\流水线通用组件_2_aluop_2 ), .Equal(alu_1_equal),
    .Result(alu_1_result), .out_6(alu_1_out_6));  // open: Result_2, out_4
  Comparator #(.width(32), .mode("twosComplement")) comparator_3 (
    .a(RegR2), .b(32'ha), .eq(comparator_3_eq));  // open: gt, lt
  and and_5 (and_5_out, ecall, comparator_3_eq);
  not not_2 (not_2_out, halt);
  \流水线通用组件  \u_流水线通用组件_3  (
    .CLK(CLK), .Clear(1'b0), .PC(EX_PC), .JALR(\流水线通用组件_2_jalr_2 ), .R1(\流水线通用组件_2_r1_2 ),
    .JAL(\流水线通用组件_2_jal_2 ), .IR(EX_IR), .R2(\流水线通用组件_2_r2_2 ), .BEQ(\流水线通用组件_2_beq_2 ),
    .PC_4(\流水线通用组件_2_pc_4_2 ), .BNE(\流水线通用组件_2_bne_2 ), .AluResult(alu_1_result),
    .MemToReg(\流水线通用组件_2_memtoreg_2 ), .MemWrite(\流水线通用组件_2_memwrite_2 ), .AluOP(\流水线通用组件_2_aluop_2 ),
    .AluSrcB(\流水线通用组件_2_alusrcb_2 ), .RegWrite(ExRegWrite), .SType(\流水线通用组件_2_stype_2 ),
    .LUI(\流水线通用组件_2_lui_2 ), .LB(\流水线通用组件_2_lb_2 ), .BLTU(\流水线通用组件_2_bltu_2 ), .ECALL(\流水线通用组件_2_ecall_2 ),
    .PC_2(M_PC), .JALR_2(\流水线通用组件_3_jalr_2 ), .R1_2(\流水线通用组件_3_r1_2 ), .JAL_2(\流水线通用组件_3_jal_2 ),
    .IR_2(MEM_IR), .R2_2(MDin), .BEQ_2(\流水线通用组件_3_beq_2 ), .PC_4_2(\流水线通用组件_3_pc_4_2 ),
    .BNE_2(\流水线通用组件_3_bne_2 ), .AluResult_2(\流水线通用组件_3_aluresult_2 ), .MemToReg_2(\流水线通用组件_3_memtoreg_2 ),
    .MemWrite_2(MemWrite), .AluOP_2(\流水线通用组件_3_aluop_2 ), .AluSrcB_2(\流水线通用组件_3_alusrcb_2 ),
    .RegWrite_2(MemRegWrite), .SType_2(\流水线通用组件_3_stype_2 ), .LUI_2(\流水线通用组件_3_lui_2 ),
    .LB_2(\流水线通用组件_3_lb_2 ), .BLTU_2(\流水线通用组件_3_bltu_2 ), .ECALL_2(\流水线通用组件_3_ecall_2 ),
    .imm12ext(\流水线通用组件_2_imm12ext_2 ), .imm12ext_2(\流水线通用组件_3_imm12ext_2 ), .BXXpc(\流水线通用组件_2_bxxpc_2 ),
    .BXXpc_2(\流水线通用组件_3_bxxpc_2 ), .JALpc(\流水线通用组件_2_jalpc_2 ), .JALpc_2(\流水线通用组件_3_jalpc_2 ),
    .Enable(\流水线通用组件_2_enable_2 ), .Enable_2(\流水线通用组件_3_enable_2 ), .Stall(1'b0));  // open: MemResult, MemResult_2, FwdR1, FwdR1_2, FwdR2, FwdR2_2
  Register #(.width(1), .trigger("falling"), .Select("low")) register_1 (
    .D(and_5_out), .en(not_2_out), .Q(halt), .clk(CLK), .clr(Go));
  not not_3 (not_3_out, halt);
  Counter #(.width(16), .max('hffff), .ongoal("stay"), .trigger("rising"), .behavior("new")) counter_2 (
    .count(not_3_out), .Q(\总周期数 ), .clk(CLK));  // open: load, D, carry, clr, preset, down
  Comparator #(.width(32), .mode("twosComplement")) comparator_4 (
    .a(RegR2), .b(32'h22), .eq(comparator_4_eq));  // open: gt, lt
  and and_6 (and_6_out, ecall, comparator_4_eq);
  RAM #(.addrWidth(10), .dataWidth(32), .bus("separate"), .Select("high")) ram_1 (
    .addr(\流水线通用组件_3_aluresult_2 [11:2]), .din(MDin), .data(ram_1_data), .str(MemWrite), .clk(CLK));  // open: sel, ld, clr
  \流水线通用组件  \u_流水线通用组件_4  (
    .CLK(CLK), .Clear(1'b0), .PC(M_PC), .JALR(\流水线通用组件_3_jalr_2 ), .R1(\流水线通用组件_3_r1_2 ),
    .JAL(\流水线通用组件_3_jal_2 ), .IR(MEM_IR), .R2(MDin), .BEQ(\流水线通用组件_3_beq_2 ), .PC_4(\流水线通用组件_3_pc_4_2 ),
    .BNE(\流水线通用组件_3_bne_2 ), .AluResult(\流水线通用组件_3_aluresult_2 ), .MemToReg(\流水线通用组件_3_memtoreg_2 ),
    .MemResult(ram_1_data), .MemWrite(MemWrite), .AluOP(\流水线通用组件_3_aluop_2 ),
    .AluSrcB(\流水线通用组件_3_alusrcb_2 ), .RegWrite(MemRegWrite), .SType(\流水线通用组件_3_stype_2 ),
    .LUI(\流水线通用组件_3_lui_2 ), .LB(\流水线通用组件_3_lb_2 ), .BLTU(\流水线通用组件_3_bltu_2 ), .ECALL(\流水线通用组件_3_ecall_2 ),
    .PC_2(WB_PC), .JALR_2(\流水线通用组件_4_jalr_2 ), .R1_2(RegR1), .JAL_2(\流水线通用组件_4_jal_2 ), .IR_2(WB_IR),
    .R2_2(RegR2), .PC_4_2(\流水线通用组件_4_pc_4_2 ), .AluResult_2(\流水线通用组件_4_aluresult_2 ),
    .MemToReg_2(\流水线通用组件_4_memtoreg_2 ), .MemResult_2(\流水线通用组件_4_memresult_2 ), .RegWrite_2(RegWrite),
    .LUI_2(\流水线通用组件_4_lui_2 ), .LB_2(\流水线通用组件_4_lb_2 ), .ECALL_2(ecall), .imm12ext(\流水线通用组件_3_imm12ext_2 ),
    .BXXpc(\流水线通用组件_3_bxxpc_2 ), .JALpc(\流水线通用组件_3_jalpc_2 ), .Enable(\流水线通用组件_3_enable_2 ), .Stall(1'b0));  // open: BEQ_2, BNE_2, MemWrite_2, AluOP_2, AluSrcB_2, SType_2, BLTU_2, imm12ext_2, BXXpc_2, JALpc_2, Enable_2, FwdR1, FwdR1_2, FwdR2, FwdR2_2
  Register #(.width(32), .trigger("rising"), .Select("low")) register_2 (
    .D(RegR1), .en(and_6_out), .Q(LedData), .clk(CLK));  // open: clr
  or or_3 (or_3_out, \流水线通用组件_4_jalr_2 , \流水线通用组件_4_jal_2 );
  Multiplexer #(.select(2), .width(8), .disabled("Z"), .enable("false")) multiplexer_7 (
    .in0(\流水线通用组件_4_memresult_2 [7:0]), .in1(\流水线通用组件_4_memresult_2 [15:8]),
    .in2(\流水线通用组件_4_memresult_2 [23:16]), .in3(\流水线通用组件_4_memresult_2 [31:24]), .out(multiplexer_7_out),
    .sel(\流水线通用组件_4_aluresult_2 [1:0]));
  assign bit_extender_4_out = {{24{multiplexer_7_out[7]}}, multiplexer_7_out};  // Bit_Extender bit_extender_4
  assign and_7_out = 32'hfffff000 & WB_IR;  // AND_Gate and_7, 32 bits wide
  Multiplexer #(.select(1), .width(32), .disabled("Z"), .enable("false")) multiplexer_8 (
    .in0(\流水线通用组件_4_memresult_2 ), .in1(bit_extender_4_out), .out(multiplexer_8_out), .sel(\流水线通用组件_4_lb_2 ));
  Multiplexer #(.select(1), .width(32), .disabled("Z"), .enable("false")) multiplexer_9 (
    .in0(\流水线通用组件_4_aluresult_2 ), .in1(multiplexer_8_out), .out(multiplexer_9_out),
    .sel(\流水线通用组件_4_memtoreg_2 ));
  Multiplexer #(.select(1), .width(32), .disabled("Z"), .enable("false")) multiplexer_10 (
    .in0(multiplexer_9_out), .in1(and_7_out), .out(multiplexer_10_out), .sel(\流水线通用组件_4_lui_2 ));
  Multiplexer #(.select(1), .width(32), .disabled("Z"), .enable("false")) multiplexer_11 (
    .in0(multiplexer_10_out), .in1(\流水线通用组件_4_pc_4_2 ), .out(RDin), .sel(or_3_out));

  // Other names for the same wires on the sheet: ExReg_num[4:0] = EX_IR[11:7]; MemReg_num[4:0] = MEM_IR[11:7];
  //   MEM_PC[31:0] = M_PC; WriteBack_Rd[4:0] = WB_IR[11:7]; WriteBack_We = RegWrite

  // Notes on the sheet:
  //   中断源
  //   时空图监测，可删除
  //   中断等待指示
  //   数码管输出
  //   contents of rom_1 (hex, n*v repeats v):
  //   100493 100006f 100493 200913 300993 100006f 100493 200913 300993 100006f 100493 200913 300993
  //   100006f 100493 200913 300993 29c000ef 100413 100493 1f49493 900533 2200893 73 24d493 48463 fedff06f
  //   900533 2200893 73 100493 249493 900533 2200893 73 48463 fedff06f 100493 1f49493 900533 2200893 73
  //   4034d493 900533 2200893 73 4044d493 900533 2200893 73 4044d493 900533 2200893 73 4044d493 900533
  //   2200893 73 4044d493 900533 2200893 73 4044d493 900533 2200893 73 4044d493 900533 2200893 73 4044d493
  //   900533 2200893 73 100413 1f41993 41f9d993 433 c00913 300b13 140413 f47413 800293 100313 499993
  //   89e9b3 1300533 2200893 73 406282b3 fe0294e3 140413 f00f93 1f47433 1c41413 800293 100313 49d993
  //   89e9b3 1300533 2200893 73 406282b3 fe0294e3 1c45413 406b0b33 b0463 f95ff06f 2b3 fff2c293 829293
  //   ff2e293 500533 2200893 73 fff00413 493 84a023 140413 448493 84a023 140413 448493 84a023 140413
  //   448493 84a023 140413 448493 84a023 140413 448493 84a023 140413 448493 84a023 140413 448493 84a023
  //   140413 448493 84a023 140413 448493 84a023 140413 448493 84a023 140413 448493 84a023 140413 448493
  //   84a023 140413 448493 84a023 140413 448493 84a023 140413 448493 84a023 140413 448493 140413 433
  //   3c00493 42983 4aa03 149a2b3 28663 134a023 1442023 ffc48493 fe9412e3 800533 2200893 73 440413 3c00493
  //   fc9416e3 a00893 73 413 140413 800533 2200893 73 240413 800533 2200893 73 340413 800533 2200893 73
  //   440413 800533 2200893 73 540413 800533 2200893 73 640413 800533 2200893 73 740413 800533 2200893 73
  //   840413 800533 2200893 2200893 73 8067
  //   控制位
  //   RS1
  //   RS2
  //   imm12
  //   流水调试日志用
  //   暂停节拍，不能为0
  //   戳工具置1进入计数暂停模式，ctrl+k时钟自动运行到对应节拍暂停
  //   ctrl+k关闭时钟连续运行，将控制位置零，进入单步调试模式调试
  //   a7
  //   a0
  //   可计数暂停的时钟源
  //   xia jiang yan
  //   为方便自动评测，需要输出流水线各段保存的PC值，注意是PC不是PC+4，另外ID段寄存器写入信息，Mem段内存写入信息也要输出
endmodule
module \重定向流水线  (
  output RegWrite,
  output MemWrite,
  output [31:0] IF_PC,
  output [31:0] ID_PC,
  output [31:0] EX_PC,
  output [31:0] M_PC,
  output [31:0] WB_PC,
  output [31:0] RDin,
  output [31:0] MDin,
  output [31:0] LedData
);

  wire alu_1_equal, alu_1_out_6, and_1_out, and_2_out, and_3_out, and_4_out, and_5_out, and_7_out, and_8_out,
       and_10_out, Bubble, CLK, clock_1_out, clock_2_out, comparator_1_gt, comparator_2_eq, comparator_2_lt,
       comparator_4_eq, comparator_5_eq, d_ff_1_q, ecall, ExRegWrite, Go, halt, IR1, IR2, IR3, LoadUse,
       MemRegWrite, nand_1_out, not_1_out, not_2_out, not_3_out, or_1_out, or_2_out, or_3_out, or_4_out,
       or_5_out, RST, SType, W1, W2, W3, \单周期硬布线控制器_1_alu_src , \单周期硬布线控制器_1_beq , \单周期硬布线控制器_1_bltu ,
       \单周期硬布线控制器_1_bne , \单周期硬布线控制器_1_ecall , \单周期硬布线控制器_1_jal , \单周期硬布线控制器_1_jalr , \单周期硬布线控制器_1_lb ,
       \单周期硬布线控制器_1_lui , \单周期硬布线控制器_1_memtoreg , \单周期硬布线控制器_1_memwrite , \单周期硬布线控制器_1_regwrite ,
       \流水线通用组件_1_enable_2 , \流水线通用组件_2_alusrcb_2 , \流水线通用组件_2_beq_2 , \流水线通用组件_2_bltu_2 , \流水线通用组件_2_bne_2 ,
       \流水线通用组件_2_ecall_2 , \流水线通用组件_2_enable_2 , \流水线通用组件_2_jal_2 , \流水线通用组件_2_jalr_2 , \流水线通用组件_2_lb_2 ,
       \流水线通用组件_2_lui_2 , \流水线通用组件_2_memtoreg_2 , \流水线通用组件_2_memwrite_2 , \流水线通用组件_2_stype_2 ,
       \流水线通用组件_3_alusrcb_2 , \流水线通用组件_3_beq_2 , \流水线通用组件_3_bltu_2 , \流水线通用组件_3_bne_2 , \流水线通用组件_3_ecall_2 ,
       \流水线通用组件_3_enable_2 , \流水线通用组件_3_jal_2 , \流水线通用组件_3_jalr_2 , \流水线通用组件_3_lb_2 , \流水线通用组件_3_lui_2 ,
       \流水线通用组件_3_memtoreg_2 , \流水线通用组件_3_stype_2 , \流水线通用组件_4_jal_2 , \流水线通用组件_4_jalr_2 , \流水线通用组件_4_lb_2 ,
       \流水线通用组件_4_lui_2 , \流水线通用组件_4_memtoreg_2 ;
  wire [1:0] ExFwd_R1, ExFwd_R2, multiplexer_5_out, multiplexer_6_out, \寄存器使用情况_1_r1exrelate ,
       \寄存器使用情况_1_r2exrelate ;
  wire [2:0] NextPCSelector;
  wire [3:0] \单周期硬布线控制器_1_alu_op , \流水线通用组件_2_aluop_2 , \流水线通用组件_3_aluop_2 ;
  wire [4:0] multiplexer_3_out, multiplexer_4_out;
  wire [7:0] multiplexer_12_out;
  wire [11:0] multiplexer_2_out;
  wire [12:0] CNT_num;
  wire [15:0] \LoadUse次数 , \总周期数 , \插入气泡数 , \无条件分支数 , \条件分支成功数 ;
  wire [31:0] adder_1_out, adder_2_out, adder_3_out, alu_1_result, and_6_out, and_9_out, and_11_out,
       bit_extender_1_out, bit_extender_2_out, bit_extender_3_out, bit_extender_4_out, EX_IR, ExOld_R1,
       ExOld_R2, ID_IR, IF_IR, MEM_IR, MemAluResult, multiplexer_1_out, multiplexer_8_out,
       multiplexer_10_out, multiplexer_13_out, multiplexer_14_out, multiplexer_15_out, R1Redirect,
       R2Redirect, ram_1_data, regifile_1_r1, regifile_1_r2, RegR1, RegR2, shifter_1_out, shifter_2_out,
       WB_IR, \流水线通用组件_1_pc_4_2 , \流水线通用组件_2_bxxpc_2 , \流水线通用组件_2_imm12ext_2 , \流水线通用组件_2_jalpc_2 ,
       \流水线通用组件_2_pc_4_2 , \流水线通用组件_3_aluresult_2 , \流水线通用组件_3_bxxpc_2 , \流水线通用组件_3_imm12ext_2 ,
       \流水线通用组件_3_jalpc_2 , \流水线通用组件_3_pc_4_2 , \流水线通用组件_3_r1_2 , \流水线通用组件_4_aluresult_2 ,
       \流水线通用组件_4_memresult_2 , \流水线通用组件_4_pc_4_2 ;

  Button \u_总复位  (.out(RST));
  Button _1 (.out(IR1));
  Button _2 (.out(IR2));
  Button _3 (.out(IR3));
  // Probe on \总周期数 
  // Probe on \总周期数 
  Button \u_继续运行  (.out(Go));
  LED #(.active("true")) led_1 (.in(W1));
  LED #(.active("true")) led_2 (.in(W2));
  LED #(.active("true")) led_3 (.in(W3));
  Hex_Digit_Display hex_digit_display_1 (.value(LedData[31:28]));  // open: dp
  // Probe on IF_PC[19:0]
  // RiscV_Probe riscv_probe_1: pin names not known; wires that end beside it: IF_IR
  Hex_Digit_Display hex_digit_display_2 (.value(LedData[27:24]));  // open: dp
  Hex_Digit_Display hex_digit_display_3 (.value(LedData[23:20]));  // open: dp
  // Probe on ID_PC[19:0]
  // RiscV_Probe riscv_probe_2: pin names not known; wires that end beside it: ID_IR
  not not_1 (not_1_out, or_1_out);
  or or_1 (or_1_out, halt, LoadUse);
  Hex_Digit_Display hex_digit_display_4 (.value(LedData[19:16]));  // open: dp
  Hex_Digit_Display hex_digit_display_5 (.value(LedData[15:12]));  // open: dp
  Register #(.width(32), .trigger("rising"), .Select("low")) PC (
    .D(multiplexer_1_out), .en(not_1_out), .Q(IF_PC), .clk(CLK), .clr(RST));
  Hex_Digit_Display hex_digit_display_6 (.value(LedData[7:4]));  // open: dp
  Hex_Digit_Display hex_digit_display_7 (.value(LedData[11:8]));  // open: dp
  Clock #(.highDuration(1), .lowDuration(1)) clock_1 (.out(clock_1_out));
  // Probe on EX_PC[19:0]
  // RiscV_Probe riscv_probe_3: pin names not known; wires that end beside it: clock_1_out, EX_IR, CLK
  Multiplexer #(.select(1), .width(32), .disabled("Z"), .enable("false")) multiplexer_1 (
    .in0(adder_1_out), .in1(multiplexer_8_out), .out(multiplexer_1_out), .sel(Bubble));
  Hex_Digit_Display hex_digit_display_8 (.value(LedData[3:0]));  // open: dp
  Counter #(.width(16), .max('hffff), .ongoal("stay"), .trigger("rising"), .behavior("old")) counter_1 (
    .Q(\条件分支成功数 ), .clk(and_1_out));  // open: load, D, count, carry, clr, preset
  and and_1 (and_1_out, ~CLK, comparator_1_gt);  // AND_Gate
  ROM #(.addrWidth(10), .dataWidth(32), .Select("high")) rom_1 (.addr(IF_PC[11:2]), .data(IF_IR));
  Adder #(.width(32)) adder_1 (.a(IF_PC), .b(32'h4), .out(adder_1_out));  // open: cin, cout
  // Probe on \总周期数 
  // Probe on M_PC[19:0]
  // RiscV_Probe riscv_probe_4: pin names not known; wires that end beside it: MEM_IR
  Comparator #(.width(3), .mode("unsigned")) comparator_1 (
    .a(NextPCSelector), .b(3'b010), .gt(comparator_1_gt));  // open: eq, lt
  // Probe on \总周期数 
  // Probe on \无条件分支数 
  // Probe on \条件分支成功数 
  // Probe on \插入气泡数 
  // Probe on \LoadUse次数 
  and and_2 (and_2_out, ~CLK, ~halt, LoadUse);  // AND_Gate
  \流水线通用组件  \u_流水线通用组件_1  (
    .CLK(CLK), .Clear(Bubble), .PC(IF_PC), .IR(IF_IR), .PC_4(adder_1_out), .PC_2(ID_PC), .IR_2(ID_IR),
    .PC_4_2(\流水线通用组件_1_pc_4_2 ), .Enable(1'b1), .Enable_2(\流水线通用组件_1_enable_2 ), .Stall(or_2_out));  // open: JALR, R1, JAL, R2, BEQ, BNE, AluResult, MemToReg, MemResult, MemWrite, AluOP, AluSrcB, RegWrite, SType, LUI, LB, BLTU, ECALL, JALR_2, R1_2, JAL_2, R2_2, BEQ_2, BNE_2, AluResult_2, MemToReg_2, MemResult_2, MemWrite_2, AluOP_2, AluSrcB_2, RegWrite_2, SType_2, LUI_2, LB_2, BLTU_2, ECALL_2, imm12ext, imm12ext_2, BXXpc, BXXpc_2, JALpc, JALpc_2, FwdR1, FwdR1_2, FwdR2, FwdR2_2
  // Probe on IF_PC[11:0]
  // Probe on WB_PC[19:0]
  // RiscV_Probe riscv_probe_5: pin names not known; wires that end beside it: WB_IR
  Counter #(.width(16), .max('hffff), .ongoal("stay"), .trigger("rising"), .behavior("old")) counter_2 (
    .Q(\LoadUse次数 ), .clk(and_2_out));  // open: load, D, count, carry, clr, preset
  or or_2 (or_2_out, LoadUse, halt);
  // Probe on EX_PC[11:0]
  // Probe on ID_PC[11:0]
  // Probe on M_PC[11:0]
  D_Flip_Flop #(.trigger("high"), .Pre_Clr_Positions("LEGACY"), .NegatePresetClear("false"), .enable("true"), .NewFFLayout("false")) d_ff_1 (.Q(d_ff_1_q));  // open: clk, D, Qn, preset, en, reset
  // Probe on 13'hc
  Multiplexer #(.select(1), .width(12), .disabled("Z"), .enable("false")) multiplexer_2 (
    .in0(ID_IR[31:20]), .in1({ID_IR[31:25], ID_IR[11:7]}), .out(multiplexer_2_out), .sel(SType));
  // Probe on WB_PC[11:0]
  Comparator #(.width(13), .mode("twosComplement")) comparator_2 (
    .a(CNT_num), .b(13'hc), .eq(comparator_2_eq), .lt(comparator_2_lt));  // open: gt
  Clock #(.highDuration(1), .lowDuration(1)) clock_2 (.out(clock_2_out));
  \单周期硬布线控制器  \u_单周期硬布线控制器_1  (
    .Funct({ID_IR[30], ID_IR[25], ID_IR[14:12]}), .OP(ID_IR[6:2]), .ALU_OP(\单周期硬布线控制器_1_alu_op ),
    .MemToReg(\单周期硬布线控制器_1_memtoreg ), .MemWrite(\单周期硬布线控制器_1_memwrite ), .ALU_SRC(\单周期硬布线控制器_1_alu_src ),
    .RegWrite(\单周期硬布线控制器_1_regwrite ), .ecall(\单周期硬布线控制器_1_ecall ), .S_type(SType),
    .Jalr(\单周期硬布线控制器_1_jalr ), .Beq(\单周期硬布线控制器_1_beq ), .JAL(\单周期硬布线控制器_1_jal ), .Bne(\单周期硬布线控制器_1_bne ),
    .BLTU(\单周期硬布线控制器_1_bltu ), .LB(\单周期硬布线控制器_1_lb ), .LUI(\单周期硬布线控制器_1_lui ), .NotNop(ID_IR[0]));
  assign bit_extender_1_out = {{20{multiplexer_2_out[11]}}, multiplexer_2_out};  // Bit_Extender bit_extender_1
  assign bit_extender_2_out = {{20{ID_IR[31]}}, {ID_IR[31], ID_IR[7], ID_IR[30:25], ID_IR[11:8]}};  // Bit_Extender bit_extender_2
  assign bit_extender_3_out = {{12{ID_IR[31]}}, {ID_IR[31], ID_IR[19:12], ID_IR[20], ID_IR[30:21]}};  // Bit_Extender bit_extender_3
  nand nand_1 (nand_1_out, d_ff_1_q, comparator_2_eq);
  Counter #(.width(13), .max('h1fff), .ongoal("stay"), .trigger("rising"), .behavior("old")) counter_3 (
    .count(comparator_2_lt), .Q(CNT_num), .clk(clock_2_out));  // open: load, D, carry, clr, preset
  Multiplexer #(.select(1), .width(5), .disabled("Z"), .enable("false")) multiplexer_3 (
    .in0(ID_IR[24:20]), .in1(5'b10001), .out(multiplexer_3_out), .sel(\单周期硬布线控制器_1_ecall ));
  Shifter #(.width(32), .shift("ll")) shifter_1 (.in(bit_extender_2_out), .\dist (5'b00001), .out(shifter_1_out));
  Shifter #(.width(32), .shift("ll")) shifter_2 (.in(bit_extender_3_out), .\dist (5'b00001), .out(shifter_2_out));
  assign CLK = nand_1_out ? clock_2_out : 1'bz;  // Controlled_Buffer controlled_buffer_1
  Multiplexer #(.select(1), .width(5), .disabled("Z"), .enable("false")) multiplexer_4 (
    .in0(ID_IR[19:15]), .in1(5'b01010), .out(multiplexer_4_out), .sel(\单周期硬布线控制器_1_ecall ));
  Adder #(.width(32)) adder_2 (.a(ID_PC), .b(shifter_1_out), .out(adder_2_out));  // open: cin, cout
  Adder #(.width(32)) adder_3 (.a(ID_PC), .b(shifter_2_out), .out(adder_3_out));  // open: cin, cout
  Pull_Resistor #(.pull(1)) pull_resistor_1 (.node(CLK));
  \寄存器使用情况  \u_寄存器使用情况_1  (
    .OP(ID_IR[6:2]), .Ex_OPCode(EX_IR[6:2]), .Funct({ID_IR[30], ID_IR[25], ID_IR[14:12]}),
    .R1(multiplexer_4_out), .R2(multiplexer_3_out), .ExRegWrite(ExRegWrite), .ExReg_num(EX_IR[11:7]),
    .MemRegWrite(MemRegWrite), .MemReg_num(MEM_IR[11:7]), .LoadUse(LoadUse),
    .R1ExRelate(\寄存器使用情况_1_r1exrelate [0]), .R2ExRelate(\寄存器使用情况_1_r2exrelate [0]),
    .R1MemRelate(\寄存器使用情况_1_r1exrelate [1]), .R2MemRelate(\寄存器使用情况_1_r2exrelate [1]));  // open: Hazzard
  Multiplexer #(.select(1), .width(2), .disabled("Z"), .enable("false")) multiplexer_5 (
    .in0(\寄存器使用情况_1_r1exrelate ), .in1(2'b00), .out(multiplexer_5_out), .sel(LoadUse));
  Multiplexer #(.select(1), .width(2), .disabled("Z"), .enable("false")) multiplexer_6 (
    .in0(\寄存器使用情况_1_r2exrelate ), .in1(2'b00), .out(multiplexer_6_out), .sel(LoadUse));
  Regifile regifile_1 (
    .Din(RDin), .Clk(CLK), .R1(regifile_1_r1), .R2(regifile_1_r2), .WE(RegWrite), .W_num(WB_IR[11:7]),
    .R1_num(multiplexer_4_out), .R2_num(multiplexer_3_out));
  Multiplexer #(.select(2), .width(32), .disabled("Z"), .enable("false")) multiplexer_7 (
    .in0(ExOld_R1), .in1(MemAluResult), .in2(RDin), .in3(MemAluResult), .out(R1Redirect), .sel(ExFwd_R1));
  Counter #(.width(16), .max('hffff), .ongoal("stay"), .trigger("rising"), .behavior("old")) counter_4 (
    .Q(\无条件分支数 ), .clk(and_3_out));  // open: load, D, count, carry, clr, preset
  and and_3 (and_3_out, ~CLK, or_4_out);  // AND_Gate
  \流水线通用组件  \u_流水线通用组件_2  (
    .CLK(CLK), .Clear(or_3_out), .PC(ID_PC), .JALR(\单周期硬布线控制器_1_jalr ), .R1(regifile_1_r1),
    .JAL(\单周期硬布线控制器_1_jal ), .IR(ID_IR), .R2(regifile_1_r2), .BEQ(\单周期硬布线控制器_1_beq ),
    .PC_4(\流水线通用组件_1_pc_4_2 ), .BNE(\单周期硬布线控制器_1_bne ), .MemToReg(\单周期硬布线控制器_1_memtoreg ),
    .MemWrite(\单周期硬布线控制器_1_memwrite ), .AluOP(\单周期硬布线控制器_1_alu_op ), .AluSrcB(\单周期硬布线控制器_1_alu_src ),
    .RegWrite(\单周期硬布线控制器_1_regwrite ), .SType(SType), .LUI(\单周期硬布线控制器_1_lui ), .LB(\单周期硬布线控制器_1_lb ),
    .BLTU(\单周期硬布线控制器_1_bltu ), .ECALL(\单周期硬布线控制器_1_ecall ), .PC_2(EX_PC), .JALR_2(\流水线通用组件_2_jalr_2 ),
    .R1_2(ExOld_R1), .JAL_2(\流水线通用组件_2_jal_2 ), .IR_2(EX_IR), .R2_2(ExOld_R2), .BEQ_2(\流水线通用组件_2_beq_2 ),
    .PC_4_2(\流水线通用组件_2_pc_4_2 ), .BNE_2(\流水线通用组件_2_bne_2 ), .MemToReg_2(\流水线通用组件_2_memtoreg_2 ),
    .MemWrite_2(\流水线通用组件_2_memwrite_2 ), .AluOP_2(\流水线通用组件_2_aluop_2 ), .AluSrcB_2(\流水线通用组件_2_alusrcb_2 ),
    .RegWrite_2(ExRegWrite), .SType_2(\流水线通用组件_2_stype_2 ), .LUI_2(\流水线通用组件_2_lui_2 ),
    .LB_2(\流水线通用组件_2_lb_2 ), .BLTU_2(\流水线通用组件_2_bltu_2 ), .ECALL_2(\流水线通用组件_2_ecall_2 ),
    .imm12ext(bit_extender_1_out), .imm12ext_2(\流水线通用组件_2_imm12ext_2 ), .BXXpc(adder_2_out),
    .BXXpc_2(\流水线通用组件_2_bxxpc_2 ), .JALpc(adder_3_out), .JALpc_2(\流水线通用组件_2_jalpc_2 ),
    .Enable(\流水线通用组件_1_enable_2 ), .Enable_2(\流水线通用组件_2_enable_2 ), .Stall(halt), .FwdR1(multiplexer_5_out),
    .FwdR1_2(ExFwd_R1), .FwdR2(multiplexer_6_out), .FwdR2_2(ExFwd_R2));  // open: AluResult, MemResult, AluResult_2, MemResult_2
  or or_3 (or_3_out, Bubble, LoadUse);
  or or_4 (or_4_out, \流水线通用组件_2_jalr_2 , \流水线通用组件_2_jal_2 );
  Multiplexer #(.select(3), .width(32), .disabled("Z"), .enable("false")) multiplexer_8 (
    .in0(\流水线通用组件_2_pc_4_2 ), .in1(and_6_out), .in2(\流水线通用组件_2_jalpc_2 ), .in3(\流水线通用组件_2_bxxpc_2 ),
    .in4(\流水线通用组件_2_bxxpc_2 ), .in5(\流水线通用组件_2_bxxpc_2 ), .out(multiplexer_8_out), .sel(NextPCSelector));  // open: in6, in7
  Multiplexer #(.select(2), .width(32), .disabled("Z"), .enable("false")) multiplexer_9 (
    .in0(ExOld_R2), .in1(MemAluResult), .in2(RDin), .in3(MemAluResult), .out(R2Redirect), .sel(ExFwd_R2));
  Priority_Encoder #(.select(3), .disabled("Z")) priority_encoder_1 (
    .in0(1'b1), .in1(\流水线通用组件_2_jalr_2 ), .in2(\流水线通用组件_2_jal_2 ), .in3(and_4_out), .in4(and_5_out),
    .in5(and_7_out), .out(NextPCSelector), .en_in(1'b1));  // open: in6, in7, gs, en_out
  and and_4 (and_4_out, \流水线通用组件_2_beq_2 , alu_1_equal);
  Multiplexer #(.select(1), .width(32), .disabled("Z"), .enable("false")) multiplexer_10 (
    .in0(R2Redirect), .in1(\流水线通用组件_2_imm12ext_2 ), .out(multiplexer_10_out), .sel(\流水线通用组件_2_alusrcb_2 ));
  and and_5 (and_5_out, \流水线通用组件_2_bne_2 , ~alu_1_equal);  // AND_Gate
  assign and_6_out = alu_1_result & 32'hfffffffe;  // AND_Gate and_6, 32 bits wide
  Comparator #(.width(3), .mode("unsigned")) comparator_3 (
    .a(NextPCSelector), .b(3'b000), .gt(Bubble));  // open: eq, lt
  and and_7 (and_7_out, \流水线通用组件_2_bltu_2 , alu_1_out_6);
  ALU alu_1 (
    .X(R1Redirect), .Y(multiplexer_10_out), .AluOP(\流水线通用组件_2_aluop_2 ), .Equal(alu_1_equal),
    .Result(alu_1_result), .out_6(alu_1_out_6));  // open: Result_2, out_4
  Comparator #(.width(32), .mode("twosComplement")) comparator_4 (
    .a(RegR2), .b(32'h22), .eq(comparator_4_eq));  // open: gt, lt
  and and_8 (and_8_out, ecall, ~comparator_4_eq);  // AND_Gate
  not not_2 (not_2_out, halt);
  \流水线通用组件  \u_流水线通用组件_3  (
    .CLK(CLK), .Clear(1'b0), .PC(EX_PC), .JALR(\流水线通用组件_2_jalr_2 ), .R1(R1Redirect), .JAL(\流水线通用组件_2_jal_2 ),
    .IR(EX_IR), .R2(R2Redirect), .BEQ(\流水线通用组件_2_beq_2 ), .PC_4(\流水线通用组件_2_pc_4_2 ), .BNE(\流水线通用组件_2_bne_2 ),
    .AluResult(alu_1_result), .MemToReg(\流水线通用组件_2_memtoreg_2 ), .MemWrite(\流水线通用组件_2_memwrite_2 ),
    .AluOP(\流水线通用组件_2_aluop_2 ), .AluSrcB(\流水线通用组件_2_alusrcb_2 ), .RegWrite(ExRegWrite),
    .SType(\流水线通用组件_2_stype_2 ), .LUI(\流水线通用组件_2_lui_2 ), .LB(\流水线通用组件_2_lb_2 ), .BLTU(\流水线通用组件_2_bltu_2 ),
    .ECALL(\流水线通用组件_2_ecall_2 ), .PC_2(M_PC), .JALR_2(\流水线通用组件_3_jalr_2 ), .R1_2(\流水线通用组件_3_r1_2 ),
    .JAL_2(\流水线通用组件_3_jal_2 ), .IR_2(MEM_IR), .R2_2(MDin), .BEQ_2(\流水线通用组件_3_beq_2 ),
    .PC_4_2(\流水线通用组件_3_pc_4_2 ), .BNE_2(\流水线通用组件_3_bne_2 ), .AluResult_2(\流水线通用组件_3_aluresult_2 ),
    .MemToReg_2(\流水线通用组件_3_memtoreg_2 ), .MemWrite_2(MemWrite), .AluOP_2(\流水线通用组件_3_aluop_2 ),
    .AluSrcB_2(\流水线通用组件_3_alusrcb_2 ), .RegWrite_2(MemRegWrite), .SType_2(\流水线通用组件_3_stype_2 ),
    .LUI_2(\流水线通用组件_3_lui_2 ), .LB_2(\流水线通用组件_3_lb_2 ), .BLTU_2(\流水线通用组件_3_bltu_2 ),
    .ECALL_2(\流水线通用组件_3_ecall_2 ), .imm12ext(\流水线通用组件_2_imm12ext_2 ), .imm12ext_2(\流水线通用组件_3_imm12ext_2 ),
    .BXXpc(\流水线通用组件_2_bxxpc_2 ), .BXXpc_2(\流水线通用组件_3_bxxpc_2 ), .JALpc(\流水线通用组件_2_jalpc_2 ),
    .JALpc_2(\流水线通用组件_3_jalpc_2 ), .Enable(\流水线通用组件_2_enable_2 ), .Enable_2(\流水线通用组件_3_enable_2 ),
    .Stall(halt));  // open: MemResult, MemResult_2, FwdR1, FwdR1_2, FwdR2, FwdR2_2
  Register #(.width(1), .trigger("falling"), .Select("low")) register_1 (
    .D(and_8_out), .en(not_2_out), .Q(halt), .clk(CLK), .clr(Go));
  not not_3 (not_3_out, halt);
  Counter #(.width(16), .max('hffff), .ongoal("stay"), .trigger("rising"), .behavior("new")) counter_5 (
    .count(not_3_out), .Q(\总周期数 ), .clk(CLK));  // open: load, D, carry, clr, preset, down
  Comparator #(.width(32), .mode("twosComplement")) comparator_5 (
    .a(RegR2), .b(32'h22), .eq(comparator_5_eq));  // open: gt, lt
  Multiplexer #(.select(1), .width(32), .disabled("Z"), .enable("false")) multiplexer_11 (
    .in0(\流水线通用组件_3_aluresult_2 ), .in1(and_9_out), .out(MemAluResult), .sel(\流水线通用组件_3_lui_2 ));
  assign and_9_out = 32'hfffff000 & MEM_IR;  // AND_Gate and_9, 32 bits wide
  and and_10 (and_10_out, ecall, comparator_5_eq);
  RAM #(.addrWidth(10), .dataWidth(32), .bus("separate"), .Select("high")) ram_1 (
    .addr(\流水线通用组件_3_aluresult_2 [11:2]), .din(MDin), .data(ram_1_data), .str(MemWrite), .clk(CLK));  // open: sel, ld, clr
  \流水线通用组件  \u_流水线通用组件_4  (
    .CLK(CLK), .Clear(1'b0), .PC(M_PC), .JALR(\流水线通用组件_3_jalr_2 ), .R1(\流水线通用组件_3_r1_2 ),
    .JAL(\流水线通用组件_3_jal_2 ), .IR(MEM_IR), .R2(MDin), .BEQ(\流水线通用组件_3_beq_2 ), .PC_4(\流水线通用组件_3_pc_4_2 ),
    .BNE(\流水线通用组件_3_bne_2 ), .AluResult(\流水线通用组件_3_aluresult_2 ), .MemToReg(\流水线通用组件_3_memtoreg_2 ),
    .MemResult(ram_1_data), .MemWrite(MemWrite), .AluOP(\流水线通用组件_3_aluop_2 ),
    .AluSrcB(\流水线通用组件_3_alusrcb_2 ), .RegWrite(MemRegWrite), .SType(\流水线通用组件_3_stype_2 ),
    .LUI(\流水线通用组件_3_lui_2 ), .LB(\流水线通用组件_3_lb_2 ), .BLTU(\流水线通用组件_3_bltu_2 ), .ECALL(\流水线通用组件_3_ecall_2 ),
    .PC_2(WB_PC), .JALR_2(\流水线通用组件_4_jalr_2 ), .R1_2(RegR1), .JAL_2(\流水线通用组件_4_jal_2 ), .IR_2(WB_IR),
    .R2_2(RegR2), .PC_4_2(\流水线通用组件_4_pc_4_2 ), .AluResult_2(\流水线通用组件_4_aluresult_2 ),
    .MemToReg_2(\流水线通用组件_4_memtoreg_2 ), .MemResult_2(\流水线通用组件_4_memresult_2 ), .RegWrite_2(RegWrite),
    .LUI_2(\流水线通用组件_4_lui_2 ), .LB_2(\流水线通用组件_4_lb_2 ), .ECALL_2(ecall), .imm12ext(\流水线通用组件_3_imm12ext_2 ),
    .BXXpc(\流水线通用组件_3_bxxpc_2 ), .JALpc(\流水线通用组件_3_jalpc_2 ), .Enable(\流水线通用组件_3_enable_2 ), .Stall(halt));  // open: BEQ_2, BNE_2, MemWrite_2, AluOP_2, AluSrcB_2, SType_2, BLTU_2, imm12ext_2, BXXpc_2, JALpc_2, Enable_2, FwdR1, FwdR1_2, FwdR2, FwdR2_2
  Register #(.width(32), .trigger("rising"), .Select("low")) register_2 (
    .D(RegR1), .en(and_10_out), .Q(LedData), .clk(CLK));  // open: clr
  or or_5 (or_5_out, \流水线通用组件_4_jalr_2 , \流水线通用组件_4_jal_2 );
  assign bit_extender_4_out = {{24{multiplexer_12_out[7]}}, multiplexer_12_out};  // Bit_Extender bit_extender_4
  Multiplexer #(.select(2), .width(8), .disabled("Z"), .enable("false")) multiplexer_12 (
    .in0(\流水线通用组件_4_memresult_2 [7:0]), .in1(\流水线通用组件_4_memresult_2 [15:8]),
    .in2(\流水线通用组件_4_memresult_2 [23:16]), .in3(\流水线通用组件_4_memresult_2 [31:24]), .out(multiplexer_12_out),
    .sel(\流水线通用组件_4_aluresult_2 [1:0]));
  assign and_11_out = 32'hfffff000 & WB_IR;  // AND_Gate and_11, 32 bits wide
  Multiplexer #(.select(1), .width(32), .disabled("Z"), .enable("false")) multiplexer_13 (
    .in0(\流水线通用组件_4_memresult_2 ), .in1(bit_extender_4_out), .out(multiplexer_13_out), .sel(\流水线通用组件_4_lb_2 ));
  Multiplexer #(.select(1), .width(32), .disabled("Z"), .enable("false")) multiplexer_14 (
    .in0(\流水线通用组件_4_aluresult_2 ), .in1(multiplexer_13_out), .out(multiplexer_14_out),
    .sel(\流水线通用组件_4_memtoreg_2 ));
  Multiplexer #(.select(1), .width(32), .disabled("Z"), .enable("false")) multiplexer_15 (
    .in0(multiplexer_14_out), .in1(and_11_out), .out(multiplexer_15_out), .sel(\流水线通用组件_4_lui_2 ));
  Multiplexer #(.select(1), .width(32), .disabled("Z"), .enable("false")) multiplexer_16 (
    .in0(multiplexer_15_out), .in1(\流水线通用组件_4_pc_4_2 ), .out(RDin), .sel(or_5_out));

  // Other names for the same wires on the sheet: ExOPCode[4:0] = EX_IR[6:2]; ExReg_num[4:0] = EX_IR[11:7];
  //   MemReg_num[4:0] = MEM_IR[11:7]; MEM_PC[31:0] = M_PC; WriteBack_Rd[4:0] = WB_IR[11:7]; WriteBack_We = RegWrite

  // Notes on the sheet:
  //   中断源
  //   时空图监测，可删除
  //   中断等待指示
  //   数码管输出
  //   contents of rom_1 (hex, n*v repeats v):
  //   100493 100006f 100493 200913 300993 100006f 100493 200913 300993 100006f 100493 200913 300993
  //   100006f 100493 200913 300993 3e8000ef 100413 100493 1f49493 900533 2200893 73 24d493 48463 fedff06f
  //   900533 2200893 73 100493 249493 900533 2200893 73 48463 fedff06f 100493 1f49493 900533 2200893 73
  //   4034d493 900533 2200893 73 4044d493 900533 2200893 73 4044d493 900533 2200893 73 4044d493 900533
  //   2200893 73 4044d493 900533 2200893 73 4044d493 900533 2200893 73 4044d493 900533 2200893 73 4044d493
  //   900533 2200893 73 100413 1f41993 41f9d993 433 c00913 300b13 140413 f47413 800293 100313 499993
  //   89e9b3 1300533 2200893 73 406282b3 fe0294e3 140413 f00f93 1f47433 1c41413 800293 100313 49d993
  //   89e9b3 1300533 2200893 73 406282b3 fe0294e3 1c45413 406b0b33 b0463 f95ff06f 2b3 fff2c293 829293
  //   ff2e293 500533 2200893 73 fff00413 493 84a023 140413 448493 84a023 140413 448493 84a023 140413
  //   448493 84a023 140413 448493 84a023 140413 448493 84a023 140413 448493 84a023 140413 448493 84a023
  //   140413 448493 84a023 140413 448493 84a023 140413 448493 84a023 140413 448493 84a023 140413 448493
  //   84a023 140413 448493 84a023 140413 448493 84a023 140413 448493 84a023 140413 448493 140413 433
  //   3c00493 42983 4aa03 149a2b3 28663 134a023 1442023 ffc48493 fe9412e3 800533 2200893 73 440413 3c00493
  //   fc9416e3 3200893 73 100293 300313 800493 849493 7648493 1449493 900533 2200893 73 800e13 54d4b3
  //   64d4b3 900533 2200893 73 fffe0e13 fe0e14e3 3200893 73 800e13 fedc04b7 fff00413 1045413 84e4b3 900533
  //   2200893 73 ba984b7 900533 73 76544b7 900533 73 32104b7 900533 73 fffe0e13 fa0e1ee3 3200893 73 313
  //   1000e13 8400493 849493 8348493 400913 891913 490913 849493 8248493 849493 8148493 891913 490913
  //   891913 490913 932023 12484b3 430313 fffe0e13 fe0e18e3 2000e13 313 30483 900533 2200893 73 130313
  //   fffe0e13 fe0e14e3 3200893 73 ff100493 900533 2200893 73 148493 fe9068e3 900533 2200893 73 a00893 73
  //   413 140413 800533 2200893 73 240413 800533 2200893 73 340413 800533 2200893 73 440413 800533 2200893
  //   73 540413 800533 2200893 73 640413 800533 2200893 73 740413 800533 2200893 73 840413 800533 2200893
  //   2200893 73 8067
  //   控制位
  //   RS1
  //   RS2
  //   imm12
  //   流水调试日志用
  //   暂停节拍，不能为0
  //   戳工具置1进入计数暂停模式，ctrl+k时钟自动运行到对应节拍暂停
  //   ctrl+k关闭时钟连续运行，将控制位置零，进入单步调试模式调试
  //   a7
  //   a0
  //   可计数暂停的时钟源
  //   xia jiang yan
  //   为方便自动评测，需要输出流水线各段保存的PC值，注意是PC不是PC+4，另外ID段寄存器写入信息，Mem段内存写入信息也要输出
endmodule

module \中断按键参考电路  (
  input  \同步清零信号 ,
  output \与中断屏蔽位与 
);

  wire \_1号中断_out , and_1_out, clock_1_out, d_ff_1_q, or_1_out, or_2_out;

  Clock #(.highDuration(1), .lowDuration(1)) clock_1 (.out(clock_1_out));
  Button \_1号中断  (.out(\_1号中断_out ));
  or or_1 (or_1_out, \与中断屏蔽位与 , d_ff_1_q);
  LED #(.active("true")) \_1号中断等待指示灯  (.in(or_1_out));
  D_Flip_Flop #(.trigger("rising"), .Pre_Clr_Positions("LEGACY"), .NegatePresetClear("false"), .enable("true"), .NewFFLayout("false")) d_ff_1 (
    .clk(\_1号中断_out ), .D(1'b1), .Q(d_ff_1_q), .reset(\与中断屏蔽位与 ));  // open: Qn, preset, en
  or or_2 (or_2_out, d_ff_1_q, \与中断屏蔽位与 );
  and and_1 (and_1_out, or_2_out, ~\同步清零信号 );  // AND_Gate
  D_Flip_Flop #(.trigger("rising"), .Pre_Clr_Positions("LEGACY"), .NegatePresetClear("false"), .enable("true"), .NewFFLayout("false")) IR1 (
    .clk(clock_1_out), .D(and_1_out), .Q(\与中断屏蔽位与 ));  // open: Qn, preset, en, reset

  // Notes on the sheet:
  //   中断信号采样参考电路
  //   Reset 
endmodule

module \单周期_单级中断  (
  input  IR1,
  input  IR2,
  input  IR3,
  output RegWrite,
  output MemWrite,
  output [31:0] PC,
  output [31:0] IR,
  output [31:0] RDin,
  output [31:0] MDin,
  output [31:0] LedData
);

  wire CLK, comparator_1_eq, comparator_2_eq, comparator_3_eq, comparator_4_eq, Go, IR1_t, IR2_t, IR3_t, IRA,
       IRB, IRC, or_1_out, W1, W2, W3;
  wire [15:0] \总周期数 ;

  Clock #(.highDuration(1), .lowDuration(1)) clock_1 (.out(CLK));
  Button _1 ();  // open: out
  Button _2 ();  // open: out
  Button _3 ();  // open: out
  Button \u_继续运行  (.out(Go));
  LED #(.active("true")) led_1 (.in(W1));
  LED #(.active("true")) led_2 (.in(W2));
  LED #(.active("true")) led_3 (.in(W3));
  Hex_Digit_Display hex_digit_display_1 (.value(LedData[31:28]));  // open: dp
  Comparator #(.width(16), .mode("twosComplement")) comparator_1 (
    .a(16'h23b), .b(\总周期数 ), .eq(comparator_1_eq));  // open: gt, lt
  Comparator #(.width(16), .mode("twosComplement")) comparator_2 (
    .a(\总周期数 ), .b(16'h1), .eq(comparator_2_eq));  // open: gt, lt
  Comparator #(.width(16), .mode("twosComplement")) comparator_3 (
    .a(\总周期数 ), .b(16'h4), .eq(comparator_3_eq));  // open: gt, lt
  Comparator #(.width(16), .mode("twosComplement")) comparator_4 (
    .a(\总周期数 ), .b(16'h7), .eq(comparator_4_eq));  // open: gt, lt
  Hex_Digit_Display hex_digit_display_2 (.value(LedData[23:20]));  // open: dp
  Hex_Digit_Display hex_digit_display_3 (.value(LedData[27:24]));  // open: dp
  or or_1 (or_1_out, comparator_1_eq, comparator_2_eq);
  assign IRA = or_1_out ? ~CLK : 1'bz;  // Controlled_Inverter controlled_inverter_1
  assign IRB = comparator_3_eq ? ~CLK : 1'bz;  // Controlled_Inverter controlled_inverter_2
  assign IRC = comparator_4_eq ? ~CLK : 1'bz;  // Controlled_Inverter controlled_inverter_3
  Hex_Digit_Display hex_digit_display_4 (.value(LedData[19:16]));  // open: dp
  Hex_Digit_Display hex_digit_display_5 (.value(LedData[15:12]));  // open: dp
  Pull_Resistor #(.pull(0)) pull_resistor_1 (.node(IRA));
  Pull_Resistor #(.pull(0)) pull_resistor_2 (.node(IRB));
  Pull_Resistor #(.pull(0)) pull_resistor_3 (.node(IRC));
  Hex_Digit_Display hex_digit_display_6 (.value(LedData[7:4]));  // open: dp
  Hex_Digit_Display hex_digit_display_7 (.value(LedData[11:8]));  // open: dp
  // Probe on \总周期数 
  Hex_Digit_Display hex_digit_display_8 (.value(LedData[3:0]));  // open: dp
  or or_2 (IR1_t, IR1, IRA);
  or or_3 (IR2_t, IR2, IRB);
  or or_4 (IR3_t, IR3, IRC);

  // Notes on the sheet:
  //   中断源
  //   中断等待指示
  //   总复位信号应将除ROM以外所有存储组件全部清零
  //   单级中断测试信号模拟器
  //   数码管输出
  //   数码管输出应该用寄存器锁存，否则显示数据只能一闪而过
  //   为方便自动评测，需要输出PC，IR，寄存器堆写如数据RDin
  //   RAM写使能MemWrite、RAM写入数据MDin等信号
endmodule

module \单周期_多级中断  (
  input  IR1,
  input  IR2,
  input  IR3,
  output RegWrite,
  output MemWrite,
  output [31:0] PC,
  output [31:0] IR,
  output [31:0] RDin,
  output [31:0] MDin,
  output [31:0] LedData
);

  wire CLK, comparator_1_eq, comparator_2_eq, comparator_3_eq, comparator_4_eq, comparator_5_eq, Go, IR1_t,
       IR2_t, IR3_t, IRA, IRB, IRC, or_1_out, or_2_out, W1, W2, W3;
  wire [15:0] \总周期数 ;

  Clock #(.highDuration(1), .lowDuration(1)) clock_1 (.out(CLK));
  Button _1 ();  // open: out
  Button _2 ();  // open: out
  Button _3 ();  // open: out
  Button \u_继续运行  (.out(Go));
  LED #(.active("true")) led_1 (.in(W1));
  LED #(.active("true")) led_2 (.in(W2));
  LED #(.active("true")) led_3 (.in(W3));
  Hex_Digit_Display hex_digit_display_1 (.value(LedData[31:28]));  // open: dp
  Comparator #(.width(16), .mode("twosComplement")) comparator_1 (
    .a(\总周期数 ), .b(16'h7), .eq(comparator_1_eq));  // open: gt, lt
  Comparator #(.width(16), .mode("twosComplement")) comparator_2 (
    .a(\总周期数 ), .b(16'h241), .eq(comparator_2_eq));  // open: gt, lt
  Hex_Digit_Display hex_digit_display_2 (.value(LedData[23:20]));  // open: dp
  Hex_Digit_Display hex_digit_display_3 (.value(LedData[27:24]));  // open: dp
  Comparator #(.width(16), .mode("twosComplement")) comparator_3 (
    .a(16'h258), .b(\总周期数 ), .eq(comparator_3_eq));  // open: gt, lt
  or or_1 (or_1_out, comparator_3_eq, comparator_4_eq);
  Comparator #(.width(16), .mode("twosComplement")) comparator_4 (
    .a(\总周期数 ), .b(16'h1), .eq(comparator_4_eq));  // open: gt, lt
  Comparator #(.width(16), .mode("twosComplement")) comparator_5 (
    .a(\总周期数 ), .b(16'h4), .eq(comparator_5_eq));  // open: gt, lt
  or or_2 (or_2_out, comparator_1_eq, comparator_2_eq);
  Hex_Digit_Display hex_digit_display_4 (.value(LedData[19:16]));  // open: dp
  Hex_Digit_Display hex_digit_display_5 (.value(LedData[15:12]));  // open: dp
  Pull_Resistor #(.pull(0)) pull_resistor_1 (.node(IRA));
  assign IRA = or_1_out ? ~CLK : 1'bz;  // Controlled_Inverter controlled_inverter_1
  Pull_Resistor #(.pull(0)) pull_resistor_2 (.node(IRB));
  assign IRB = comparator_5_eq ? ~CLK : 1'bz;  // Controlled_Inverter controlled_inverter_2
  Pull_Resistor #(.pull(0)) pull_resistor_3 (.node(IRC));
  assign IRC = or_2_out ? ~CLK : 1'bz;  // Controlled_Inverter controlled_inverter_3
  Hex_Digit_Display hex_digit_display_6 (.value(LedData[7:4]));  // open: dp
  Hex_Digit_Display hex_digit_display_7 (.value(LedData[11:8]));  // open: dp
  // Probe on \总周期数 
  Hex_Digit_Display hex_digit_display_8 (.value(LedData[3:0]));  // open: dp
  or or_3 (IR1_t, IR1, IRA);
  or or_4 (IR2_t, IR2, IRB);
  or or_5 (IR3_t, IR3, IRC);

  // Notes on the sheet:
  //   中断源
  //   中断等待指示
  //   总复位信号应将除ROM以外所有存储组件全部清零
  //   多级中断测试信号模拟器
  //   数码管输出
  //   数码管输出应该用寄存器锁存，否则显示数据只能一闪而过
  //   为方便自动评测，需要输出PC，IR，寄存器堆写如数据RDin
  //   RAM写使能MemWrite、RAM写入数据MDin等信号
endmodule

module \封装正确性测试  (
);

  wire IR1, IR2, IR3, MemW, RegW;
  wire [31:0] EX_PC, ID_PC, IF_PC, IR, LED, MDin, MDinr, MEM_PC, PC, RDin, RDinr, WB_PC;

  \单周期RISC_V  \u_单周期risc_v_1  (
    .IR1(IR1), .IR2(IR2), .IR3(IR3), .RegWrite(RegW), .MemWrite(MemW), .PC(PC), .IR(IR), .RDin(RDin),
    .MDin(MDin), .LedData(LED));
  \气泡流水线  \u_气泡流水线_1  (
    .RegWrite(RegW), .MemWrite(MemW), .IF_PC(IF_PC), .ID_PC(ID_PC), .EX_PC(EX_PC), .M_PC(MEM_PC),
    .WB_PC(WB_PC), .RDin(RDinr), .MDin(MDinr), .LedData(LED));
  \单周期_单级中断  \u_单周期_单级中断_1  (
    .IR1(IR1), .IR2(IR2), .IR3(IR3), .RegWrite(RegW), .MemWrite(MemW), .PC(PC), .IR(IR), .RDin(RDin),
    .MDin(MDin), .LedData(LED));
  \理想流水线  \u_理想流水线_1  (
    .RegWrite(RegW), .MemWrite(MemW), .IF_PC(IF_PC), .ID_PC(ID_PC), .EX_PC(EX_PC), .M_PC(MEM_PC),
    .WB_PC(WB_PC), .RDin(RDinr), .MDin(MDinr), .LedData(LED));
  \重定向流水线  \u_重定向流水线_1  (
    .RegWrite(RegW), .MemWrite(MemW), .IF_PC(IF_PC), .ID_PC(ID_PC), .EX_PC(EX_PC), .M_PC(MEM_PC),
    .WB_PC(WB_PC), .RDin(RDinr), .MDin(MDinr), .LedData(LED));
  \单周期_多级中断  \u_单周期_多级中断_1  (
    .IR1(IR1), .IR2(IR2), .IR3(IR3), .RegWrite(RegW), .MemWrite(MemW), .PC(PC), .IR(IR), .RDin(RDin),
    .MDin(MDin), .LedData(LED));

  // Notes on the sheet:
  //   单周期封装测试
  //   气泡流水封装测试
  //   单周期+单级中断封装测试
  //   请检查上面封装有无位宽不匹配，引脚标签是否和连接的标签相对应，否则无法在educoder平台上正确测试
  //   理想流水封装测试
  //   重定向流水封装测试
  //   单周期+多级中断封装测试
endmodule

module \流水线通用组件  (
  input  CLK,
  input  Clear,
  input  Enable,
  input  Stall,
  input  [31:0] PC,
  input  JALR,
  input  [31:0] R1,
  input  JAL,
  input  [31:0] IR,
  input  [31:0] R2,
  input  BEQ,
  input  [31:0] PC_4,
  input  BNE,
  input  [31:0] AluResult,
  input  MemToReg,
  input  [31:0] MemResult,
  input  MemWrite,
  input  [31:0] imm12ext,
  input  [3:0] AluOP,
  input  [31:0] BXXpc,
  input  AluSrcB,
  input  RegWrite,
  input  [31:0] JALpc,
  input  SType,
  input  [1:0] FwdR1,
  input  LUI,
  input  [1:0] FwdR2,
  input  LB,
  input  BLTU,
  input  ECALL,
  output Enable_2,
  output [31:0] PC_2,
  output JALR_2,
  output [31:0] R1_2,
  output JAL_2,
  output [31:0] IR_2,
  output [31:0] R2_2,
  output BEQ_2,
  output [31:0] PC_4_2,
  output BNE_2,
  output [31:0] AluResult_2,
  output MemToReg_2,
  output [31:0] MemResult_2,
  output MemWrite_2,
  output [31:0] imm12ext_2,
  output [3:0] AluOP_2,
  output [31:0] BXXpc_2,
  output AluSrcB_2,
  output RegWrite_2,
  output [31:0] JALpc_2,
  output SType_2,
  output [1:0] FwdR1_2,
  output LUI_2,
  output [1:0] FwdR2_2,
  output LB_2,
  output BLTU_2,
  output ECALL_2
);

  wire and_1_out, EN, multiplexer_4_out, multiplexer_5_out, multiplexer_6_out, multiplexer_7_out,
       multiplexer_8_out, multiplexer_9_out, multiplexer_11_out, multiplexer_12_out, multiplexer_13_out,
       multiplexer_14_out, multiplexer_15_out, multiplexer_16_out, multiplexer_17_out, or_1_out;
  wire [1:0] multiplexer_25_out, multiplexer_26_out;
  wire [3:0] multiplexer_10_out;
  wire [31:0] multiplexer_1_out, multiplexer_2_out, multiplexer_3_out, multiplexer_18_out,
       multiplexer_19_out, multiplexer_20_out, multiplexer_21_out, multiplexer_22_out, multiplexer_23_out,
       multiplexer_24_out;

  and and_1 (and_1_out, ~Clear, ~Stall);  // AND_Gate
  Multiplexer #(.select(1), .width(32), .disabled("Z"), .enable("false")) multiplexer_1 (
    .in0(PC), .in1({32{1'b0}}), .out(multiplexer_1_out), .sel(Clear));
  Multiplexer #(.select(1), .width(32), .disabled("Z"), .enable("false")) multiplexer_2 (
    .in0(IR), .in1({32{1'b0}}), .out(multiplexer_2_out), .sel(Clear));
  Multiplexer #(.select(1), .width(32), .disabled("Z"), .enable("false")) multiplexer_3 (
    .in0(PC_4), .in1({32{1'b0}}), .out(multiplexer_3_out), .sel(Clear));
  or or_1 (or_1_out, Clear, and_1_out);
  Register #(.width(32), .trigger("rising"), .Select("low")) register_1 (
    .D(multiplexer_1_out), .en(EN), .Q(PC_2), .clk(CLK));  // open: clr
  Register #(.width(32), .trigger("rising"), .Select("low")) register_2 (
    .D(multiplexer_2_out), .en(EN), .Q(IR_2), .clk(CLK));  // open: clr
  Register #(.width(32), .trigger("rising"), .Select("low")) register_3 (
    .D(multiplexer_3_out), .en(EN), .Q(PC_4_2), .clk(CLK));  // open: clr
  and and_2 (EN, Enable, or_1_out);
  Register #(.width(1), .trigger("rising"), .Select("low")) register_4 (
    .D(1'b1), .en(Enable), .Q(Enable_2), .clk(CLK));  // open: clr
  Multiplexer #(.select(1), .width(1), .disabled("Z"), .enable("false")) multiplexer_4 (
    .in0(JALR), .in1(1'b0), .out(multiplexer_4_out), .sel(Clear));
  Multiplexer #(.select(1), .width(1), .disabled("Z"), .enable("false")) multiplexer_5 (
    .in0(JAL), .in1(1'b0), .out(multiplexer_5_out), .sel(Clear));
  Multiplexer #(.select(1), .width(1), .disabled("Z"), .enable("false")) multiplexer_6 (
    .in0(BEQ), .in1(1'b0), .out(multiplexer_6_out), .sel(Clear));
  Multiplexer #(.select(1), .width(1), .disabled("Z"), .enable("false")) multiplexer_7 (
    .in0(BNE), .in1(1'b0), .out(multiplexer_7_out), .sel(Clear));
  Multiplexer #(.select(1), .width(1), .disabled("Z"), .enable("false")) multiplexer_8 (
    .in0(MemToReg), .in1(1'b0), .out(multiplexer_8_out), .sel(Clear));
  Multiplexer #(.select(1), .width(1), .disabled("Z"), .enable("false")) multiplexer_9 (
    .in0(MemWrite), .in1(1'b0), .out(multiplexer_9_out), .sel(Clear));
  Multiplexer #(.select(1), .width(4), .disabled("Z"), .enable("false")) multiplexer_10 (
    .in0(AluOP), .in1(4'b0000), .out(multiplexer_10_out), .sel(Clear));
  Multiplexer #(.select(1), .width(1), .disabled("Z"), .enable("false")) multiplexer_11 (
    .in0(AluSrcB), .in1(1'b0), .out(multiplexer_11_out), .sel(Clear));
  Multiplexer #(.select(1), .width(1), .disabled("Z"), .enable("false")) multiplexer_12 (
    .in0(RegWrite), .in1(1'b0), .out(multiplexer_12_out), .sel(Clear));
  Multiplexer #(.select(1), .width(1), .disabled("Z"), .enable("false")) multiplexer_13 (
    .in0(SType), .in1(1'b0), .out(multiplexer_13_out), .sel(Clear));
  Multiplexer #(.select(1), .width(1), .disabled("Z"), .enable("false")) multiplexer_14 (
    .in0(LUI), .in1(1'b0), .out(multiplexer_14_out), .sel(Clear));
  Multiplexer #(.select(1), .width(1), .disabled("Z"), .enable("false")) multiplexer_15 (
    .in0(LB), .in1(1'b0), .out(multiplexer_15_out), .sel(Clear));
  Multiplexer #(.select(1), .width(1), .disabled("Z"), .enable("false")) multiplexer_16 (
    .in0(BLTU), .in1(1'b0), .out(multiplexer_16_out), .sel(Clear));
  Multiplexer #(.select(1), .width(1), .disabled("Z"), .enable("false")) multiplexer_17 (
    .in0(ECALL), .in1(1'b0), .out(multiplexer_17_out), .sel(Clear));
  Register #(.width(1), .trigger("rising"), .Select("low")) register_5 (
    .D(multiplexer_4_out), .en(EN), .Q(JALR_2), .clk(CLK));  // open: clr
  Register #(.width(1), .trigger("rising"), .Select("low")) register_6 (
    .D(multiplexer_5_out), .en(EN), .Q(JAL_2), .clk(CLK));  // open: clr
  Register #(.width(1), .trigger("rising"), .Select("low")) register_7 (
    .D(multiplexer_6_out), .en(EN), .Q(BEQ_2), .clk(CLK));  // open: clr
  Register #(.width(1), .trigger("rising"), .Select("low")) register_8 (
    .D(multiplexer_7_out), .en(EN), .Q(BNE_2), .clk(CLK));  // open: clr
  Register #(.width(1), .trigger("rising"), .Select("low")) register_9 (
    .D(multiplexer_8_out), .en(EN), .Q(MemToReg_2), .clk(CLK));  // open: clr
  Register #(.width(1), .trigger("rising"), .Select("low")) register_10 (
    .D(multiplexer_9_out), .en(EN), .Q(MemWrite_2), .clk(CLK));  // open: clr
  Register #(.width(4), .trigger("rising"), .Select("low")) register_11 (
    .D(multiplexer_10_out), .en(EN), .Q(AluOP_2), .clk(CLK));  // open: clr
  Register #(.width(1), .trigger("rising"), .Select("low")) register_12 (
    .D(multiplexer_11_out), .en(EN), .Q(AluSrcB_2), .clk(CLK));  // open: clr
  Register #(.width(1), .trigger("rising"), .Select("low")) register_13 (
    .D(multiplexer_12_out), .en(EN), .Q(RegWrite_2), .clk(CLK));  // open: clr
  Register #(.width(1), .trigger("rising"), .Select("low")) register_14 (
    .D(multiplexer_13_out), .en(EN), .Q(SType_2), .clk(CLK));  // open: clr
  Register #(.width(1), .trigger("rising"), .Select("low")) register_15 (
    .D(multiplexer_14_out), .en(EN), .Q(LUI_2), .clk(CLK));  // open: clr
  Register #(.width(1), .trigger("rising"), .Select("low")) register_16 (
    .D(multiplexer_15_out), .en(EN), .Q(LB_2), .clk(CLK));  // open: clr
  Register #(.width(1), .trigger("rising"), .Select("low")) register_17 (
    .D(multiplexer_16_out), .en(EN), .Q(BLTU_2), .clk(CLK));  // open: clr
  Register #(.width(1), .trigger("rising"), .Select("low")) register_18 (
    .D(multiplexer_17_out), .en(EN), .Q(ECALL_2), .clk(CLK));  // open: clr
  Multiplexer #(.select(1), .width(32), .disabled("Z"), .enable("false")) multiplexer_18 (
    .in0(R1), .in1({32{1'b0}}), .out(multiplexer_18_out), .sel(Clear));
  Multiplexer #(.select(1), .width(32), .disabled("Z"), .enable("false")) multiplexer_19 (
    .in0(R2), .in1({32{1'b0}}), .out(multiplexer_19_out), .sel(Clear));
  Multiplexer #(.select(1), .width(32), .disabled("Z"), .enable("false")) multiplexer_20 (
    .in0(AluResult), .in1({32{1'b0}}), .out(multiplexer_20_out), .sel(Clear));
  Multiplexer #(.select(1), .width(32), .disabled("Z"), .enable("false")) multiplexer_21 (
    .in0(MemResult), .in1({32{1'b0}}), .out(multiplexer_21_out), .sel(Clear));
  Multiplexer #(.select(1), .width(32), .disabled("Z"), .enable("false")) multiplexer_22 (
    .in0(imm12ext), .in1({32{1'b0}}), .out(multiplexer_22_out), .sel(Clear));
  Multiplexer #(.select(1), .width(32), .disabled("Z"), .enable("false")) multiplexer_23 (
    .in0(BXXpc), .in1({32{1'b0}}), .out(multiplexer_23_out), .sel(Clear));
  Multiplexer #(.select(1), .width(32), .disabled("Z"), .enable("false")) multiplexer_24 (
    .in0(JALpc), .in1({32{1'b0}}), .out(multiplexer_24_out), .sel(Clear));
  Multiplexer #(.select(1), .width(2), .disabled("Z"), .enable("false")) multiplexer_25 (
    .in0(FwdR1), .in1(2'b00), .out(multiplexer_25_out), .sel(Clear));
  Multiplexer #(.select(1), .width(2), .disabled("Z"), .enable("false")) multiplexer_26 (
    .in0(FwdR2), .in1(2'b00), .out(multiplexer_26_out), .sel(Clear));
  Register #(.width(32), .trigger("rising"), .Select("low")) register_19 (
    .D(multiplexer_18_out), .en(EN), .Q(R1_2), .clk(CLK));  // open: clr
  Register #(.width(32), .trigger("rising"), .Select("low")) register_20 (
    .D(multiplexer_19_out), .en(EN), .Q(R2_2), .clk(CLK));  // open: clr
  Register #(.width(32), .trigger("rising"), .Select("low")) register_21 (
    .D(multiplexer_20_out), .en(EN), .Q(AluResult_2), .clk(CLK));  // open: clr
  Register #(.width(32), .trigger("rising"), .Select("low")) register_22 (
    .D(multiplexer_21_out), .en(EN), .Q(MemResult_2), .clk(CLK));  // open: clr
  Register #(.width(32), .trigger("rising"), .Select("low")) register_23 (
    .D(multiplexer_22_out), .en(EN), .Q(imm12ext_2), .clk(CLK));  // open: clr
  Register #(.width(32), .trigger("rising"), .Select("low")) register_24 (
    .D(multiplexer_23_out), .en(EN), .Q(BXXpc_2), .clk(CLK));  // open: clr
  Register #(.width(32), .trigger("rising"), .Select("low")) register_25 (
    .D(multiplexer_24_out), .en(EN), .Q(JALpc_2), .clk(CLK));  // open: clr
  Register #(.width(2), .trigger("rising"), .Select("low")) register_26 (
    .D(multiplexer_25_out), .en(EN), .Q(FwdR1_2), .clk(CLK));  // open: clr
  Register #(.width(2), .trigger("rising"), .Select("low")) register_27 (
    .D(multiplexer_26_out), .en(EN), .Q(FwdR2_2), .clk(CLK));  // open: clr
endmodule

module \寄存器使用情况自动生成  (
  input  OP2,
  input  OP3,
  input  OP4,
  input  OP5,
  input  OP6,
  input  F12,
  input  F13,
  input  F14,
  input  F25,
  input  F30,
  output R1Use,
  output R2Use
);

  wire and_1_out, and_2_out, and_3_out, and_4_out, and_5_out, and_6_out, and_7_out, and_8_out, and_9_out,
       and_10_out, and_11_out, and_12_out, and_13_out, and_14_out, and_15_out, and_16_out, and_17_out,
       and_18_out, and_19_out, and_20_out, and_21_out, and_22_out, and_23_out, and_24_out, and_25_out,
       and_26_out, and_27_out, and_28_out, and_29_out, and_30_out, and_31_out, and_32_out, and_33_out,
       and_34_out, and_35_out, not_1_out, not_2_out, not_3_out, not_4_out, not_5_out, not_6_out, not_7_out,
       not_8_out, not_9_out, not_10_out, not_11_out, not_12_out, not_13_out, not_14_out, not_15_out,
       not_16_out, not_17_out, not_18_out, not_19_out, not_20_out, not_21_out, not_22_out, not_23_out,
       not_24_out, not_25_out, not_26_out, not_27_out, not_28_out, not_29_out, not_30_out, not_31_out,
       not_32_out, not_33_out, not_34_out, not_35_out, not_36_out, not_37_out, not_38_out, not_39_out,
       not_40_out, not_41_out, not_42_out, not_43_out, not_44_out, not_45_out, not_46_out, not_47_out,
       not_48_out, not_49_out, not_50_out, not_51_out, not_52_out, not_53_out, not_54_out, not_55_out,
       not_56_out, not_57_out, not_58_out, not_59_out, not_60_out, not_61_out, not_62_out, not_63_out,
       not_64_out, not_65_out, not_66_out, not_67_out, not_68_out, not_69_out, not_70_out, not_71_out,
       not_72_out, not_73_out, not_74_out, not_75_out, not_76_out, not_77_out, not_78_out, not_79_out,
       not_80_out, not_81_out, not_82_out, not_83_out, not_84_out, not_85_out, not_86_out, not_87_out,
       not_88_out, not_89_out, not_90_out, not_91_out, not_92_out, not_93_out, not_94_out, not_95_out,
       not_96_out, not_97_out, not_98_out, not_99_out, not_100_out, not_101_out, not_102_out, not_103_out,
       not_104_out, not_105_out, not_106_out, not_107_out, not_108_out, not_109_out, not_110_out,
       not_111_out, not_112_out, not_113_out, not_114_out, not_115_out, not_116_out, not_117_out,
       not_118_out, not_119_out, not_120_out, not_121_out, not_122_out, not_123_out, not_124_out,
       not_125_out, not_126_out, not_127_out, not_128_out, not_129_out, not_130_out, not_131_out,
       not_132_out, not_133_out, not_134_out, not_135_out, not_136_out, not_137_out, not_138_out,
       not_139_out, not_140_out, not_141_out, not_142_out, not_143_out, not_144_out, not_145_out,
       not_146_out, not_147_out, not_148_out, not_149_out, not_150_out, not_151_out, not_152_out,
       not_153_out, not_154_out, not_155_out, not_156_out, not_157_out, not_158_out, not_159_out,
       not_160_out, not_161_out, not_162_out, not_163_out, not_164_out, not_165_out, not_166_out,
       not_167_out, not_168_out, not_169_out, not_170_out, not_171_out, not_172_out, not_173_out,
       not_174_out, not_175_out, not_176_out, not_177_out, not_178_out, not_179_out, not_180_out,
       not_181_out, not_182_out, not_183_out, not_184_out, not_185_out, not_186_out, not_187_out,
       not_188_out, not_189_out, not_190_out, not_191_out, not_192_out, not_193_out, not_194_out,
       not_195_out, not_196_out, not_197_out, not_198_out, not_199_out, not_200_out, not_201_out,
       not_202_out, not_203_out, not_204_out, not_205_out, not_206_out, not_207_out, not_208_out,
       not_209_out, not_210_out, not_211_out, not_212_out, not_213_out, not_214_out, not_215_out;

  not not_1 (not_1_out, F30);
  not not_2 (not_2_out, F25);
  not not_3 (not_3_out, F14);
  not not_4 (not_4_out, F13);
  not not_5 (not_5_out, F12);
  not not_6 (not_6_out, OP6);
  not not_7 (not_7_out, OP3);
  not not_8 (not_8_out, OP2);
  not not_9 (not_9_out, F25);
  not not_10 (not_10_out, F14);
  not not_11 (not_11_out, F13);
  not not_12 (not_12_out, F12);
  not not_13 (not_13_out, OP6);
  not not_14 (not_14_out, OP3);
  not not_15 (not_15_out, OP2);
  not not_16 (not_16_out, F30);
  not not_17 (not_17_out, F25);
  not not_18 (not_18_out, OP6);
  not not_19 (not_19_out, OP3);
  not not_20 (not_20_out, OP2);
  not not_21 (not_21_out, F30);
  not not_22 (not_22_out, F25);
  not not_23 (not_23_out, F12);
  not not_24 (not_24_out, OP6);
  not not_25 (not_25_out, OP3);
  not not_26 (not_26_out, OP2);
  not not_27 (not_27_out, F30);
  not not_28 (not_28_out, F25);
  not not_29 (not_29_out, F14);
  not not_30 (not_30_out, F12);
  not not_31 (not_31_out, OP6);
  not not_32 (not_32_out, OP3);
  not not_33 (not_33_out, OP2);
  not not_34 (not_34_out, F30);
  not not_35 (not_35_out, F25);
  not not_36 (not_36_out, F14);
  not not_37 (not_37_out, OP6);
  not not_38 (not_38_out, OP3);
  not not_39 (not_39_out, OP2);
  not not_40 (not_40_out, F14);
  not not_41 (not_41_out, F13);
  not not_42 (not_42_out, F12);
  not not_43 (not_43_out, OP6);
  not not_44 (not_44_out, OP5);
  not not_45 (not_45_out, OP3);
  not not_46 (not_46_out, OP2);
  not not_47 (not_47_out, OP6);
  not not_48 (not_48_out, OP5);
  not not_49 (not_49_out, OP3);
  not not_50 (not_50_out, OP2);
  not not_51 (not_51_out, F12);
  not not_52 (not_52_out, OP6);
  not not_53 (not_53_out, OP5);
  not not_54 (not_54_out, OP3);
  not not_55 (not_55_out, OP2);
  not not_56 (not_56_out, F13);
  not not_57 (not_57_out, F12);
  not not_58 (not_58_out, OP6);
  not not_59 (not_59_out, OP5);
  not not_60 (not_60_out, OP3);
  not not_61 (not_61_out, OP2);
  not not_62 (not_62_out, F14);
  not not_63 (not_63_out, F12);
  not not_64 (not_64_out, OP6);
  not not_65 (not_65_out, OP5);
  not not_66 (not_66_out, OP3);
  not not_67 (not_67_out, OP2);
  not not_68 (not_68_out, F30);
  not not_69 (not_69_out, F25);
  not not_70 (not_70_out, F14);
  not not_71 (not_71_out, F13);
  not not_72 (not_72_out, OP6);
  not not_73 (not_73_out, OP5);
  not not_74 (not_74_out, OP3);
  not not_75 (not_75_out, OP2);
  not not_76 (not_76_out, F30);
  not not_77 (not_77_out, F25);
  not not_78 (not_78_out, F13);
  not not_79 (not_79_out, OP6);
  not not_80 (not_80_out, OP5);
  not not_81 (not_81_out, OP3);
  not not_82 (not_82_out, OP2);
  not not_83 (not_83_out, F25);
  not not_84 (not_84_out, F13);
  not not_85 (not_85_out, OP6);
  not not_86 (not_86_out, OP5);
  not not_87 (not_87_out, OP3);
  not not_88 (not_88_out, OP2);
  not not_89 (not_89_out, F14);
  not not_90 (not_90_out, F12);
  not not_91 (not_91_out, OP6);
  not not_92 (not_92_out, OP5);
  not not_93 (not_93_out, OP4);
  not not_94 (not_94_out, OP3);
  not not_95 (not_95_out, OP2);
  not not_96 (not_96_out, F14);
  not not_97 (not_97_out, F12);
  not not_98 (not_98_out, OP6);
  not not_99 (not_99_out, OP4);
  not not_100 (not_100_out, OP3);
  not not_101 (not_101_out, OP2);
  not not_102 (not_102_out, F30);
  not not_103 (not_103_out, F25);
  not not_104 (not_104_out, F14);
  not not_105 (not_105_out, F13);
  not not_106 (not_106_out, F12);
  not not_107 (not_107_out, OP3);
  not not_108 (not_108_out, OP2);
  not not_109 (not_109_out, F14);
  not not_110 (not_110_out, F13);
  not not_111 (not_111_out, F12);
  not not_112 (not_112_out, OP4);
  not not_113 (not_113_out, OP3);
  not not_114 (not_114_out, OP2);
  not not_115 (not_115_out, F14);
  not not_116 (not_116_out, F13);
  not not_117 (not_117_out, OP4);
  not not_118 (not_118_out, OP3);
  not not_119 (not_119_out, OP2);
  not not_120 (not_120_out, F14);
  not not_121 (not_121_out, F13);
  not not_122 (not_122_out, F12);
  not not_123 (not_123_out, OP4);
  not not_124 (not_124_out, OP3);
  not not_125 (not_125_out, F30);
  not not_126 (not_126_out, F25);
  not not_127 (not_127_out, F13);
  not not_128 (not_128_out, OP6);
  not not_129 (not_129_out, OP3);
  not not_130 (not_130_out, OP2);
  not not_131 (not_131_out, F14);
  not not_132 (not_132_out, F13);
  not not_133 (not_133_out, F12);
  not not_134 (not_134_out, OP6);
  not not_135 (not_135_out, OP5);
  not not_136 (not_136_out, OP4);
  not not_137 (not_137_out, OP3);
  not not_138 (not_138_out, OP2);
  not not_139 (not_139_out, F12);
  not not_140 (not_140_out, OP4);
  not not_141 (not_141_out, OP3);
  not not_142 (not_142_out, OP2);
  not not_143 (not_143_out, F30);
  not not_144 (not_144_out, F25);
  not not_145 (not_145_out, F14);
  not not_146 (not_146_out, F13);
  not not_147 (not_147_out, F12);
  not not_148 (not_148_out, OP6);
  not not_149 (not_149_out, OP3);
  not not_150 (not_150_out, OP2);
  not not_151 (not_151_out, F25);
  not not_152 (not_152_out, F14);
  not not_153 (not_153_out, F13);
  not not_154 (not_154_out, F12);
  not not_155 (not_155_out, OP6);
  not not_156 (not_156_out, OP3);
  not not_157 (not_157_out, OP2);
  not not_158 (not_158_out, F30);
  not not_159 (not_159_out, F25);
  not not_160 (not_160_out, OP6);
  not not_161 (not_161_out, OP3);
  not not_162 (not_162_out, OP2);
  not not_163 (not_163_out, F30);
  not not_164 (not_164_out, F25);
  not not_165 (not_165_out, F12);
  not not_166 (not_166_out, OP6);
  not not_167 (not_167_out, OP3);
  not not_168 (not_168_out, OP2);
  not not_169 (not_169_out, F30);
  not not_170 (not_170_out, F25);
  not not_171 (not_171_out, F14);
  not not_172 (not_172_out, F12);
  not not_173 (not_173_out, OP6);
  not not_174 (not_174_out, OP3);
  not not_175 (not_175_out, OP2);
  not not_176 (not_176_out, F30);
  not not_177 (not_177_out, F25);
  not not_178 (not_178_out, F14);
  not not_179 (not_179_out, OP6);
  not not_180 (not_180_out, OP3);
  not not_181 (not_181_out, OP2);
  not not_182 (not_182_out, F14);
  not not_183 (not_183_out, F12);
  not not_184 (not_184_out, OP6);
  not not_185 (not_185_out, OP4);
  not not_186 (not_186_out, OP3);
  not not_187 (not_187_out, OP2);
  not not_188 (not_188_out, F30);
  not not_189 (not_189_out, F25);
  not not_190 (not_190_out, F14);
  not not_191 (not_191_out, F13);
  not not_192 (not_192_out, F12);
  not not_193 (not_193_out, OP3);
  not not_194 (not_194_out, OP2);
  not not_195 (not_195_out, F14);
  not not_196 (not_196_out, F13);
  not not_197 (not_197_out, F12);
  not not_198 (not_198_out, OP4);
  not not_199 (not_199_out, OP3);
  not not_200 (not_200_out, OP2);
  not not_201 (not_201_out, F14);
  not not_202 (not_202_out, F13);
  not not_203 (not_203_out, OP4);
  not not_204 (not_204_out, OP3);
  not not_205 (not_205_out, OP2);
  not not_206 (not_206_out, F30);
  not not_207 (not_207_out, F25);
  not not_208 (not_208_out, F13);
  not not_209 (not_209_out, OP6);
  not not_210 (not_210_out, OP3);
  not not_211 (not_211_out, OP2);
  not not_212 (not_212_out, F12);
  not not_213 (not_213_out, OP4);
  not not_214 (not_214_out, OP3);
  not not_215 (not_215_out, OP2);
  and and_1 (and_1_out, not_1_out, not_2_out, not_3_out, not_4_out, not_5_out, not_6_out, OP5, OP4, not_7_out, not_8_out);
  and and_2 (and_2_out, F30, not_9_out, not_10_out, not_11_out, not_12_out, not_13_out, OP5, OP4, not_14_out, not_15_out);
  and and_3 (and_3_out, not_16_out, not_17_out, F14, F13, F12, not_18_out, OP5, OP4, not_19_out, not_20_out);
  and and_4 (and_4_out, not_21_out, not_22_out, F14, F13, not_23_out, not_24_out, OP5, OP4, not_25_out, not_26_out);
  and and_5 (and_5_out, not_27_out, not_28_out, not_29_out, F13, not_30_out, not_31_out, OP5, OP4, not_32_out, not_33_out);
  and and_6 (and_6_out, not_34_out, not_35_out, not_36_out, F13, F12, not_37_out, OP5, OP4, not_38_out, not_39_out);
  and and_7 (and_7_out, not_40_out, not_41_out, not_42_out, not_43_out, not_44_out, OP4, not_45_out, not_46_out);
  and and_8 (and_8_out, F14, F13, F12, not_47_out, not_48_out, OP4, not_49_out, not_50_out);
  and and_9 (and_9_out, F14, F13, not_51_out, not_52_out, not_53_out, OP4, not_54_out, not_55_out);
  and and_10 (and_10_out, F14, not_56_out, not_57_out, not_58_out, not_59_out, OP4, not_60_out, not_61_out);
  and and_11 (and_11_out, not_62_out, F13, not_63_out, not_64_out, not_65_out, OP4, not_66_out, not_67_out);
  and and_12 (and_12_out, not_68_out, not_69_out, not_70_out, not_71_out, F12, not_72_out, not_73_out, OP4, not_74_out, not_75_out);
  and and_13 (and_13_out, not_76_out, not_77_out, F14, not_78_out, F12, not_79_out, not_80_out, OP4, not_81_out, not_82_out);
  and and_14 (and_14_out, F30, not_83_out, F14, not_84_out, F12, not_85_out, not_86_out, OP4, not_87_out, not_88_out);
  and and_15 (and_15_out, not_89_out, F13, not_90_out, not_91_out, not_92_out, not_93_out, not_94_out, not_95_out);
  and and_16 (and_16_out, not_96_out, F13, not_97_out, not_98_out, OP5, not_99_out, not_100_out, not_101_out);
  and and_17 (and_17_out, not_102_out, not_103_out, not_104_out, not_105_out, not_106_out, OP6, OP5, OP4, not_107_out, not_108_out);
  and and_18 (and_18_out, not_109_out, not_110_out, not_111_out, OP6, OP5, not_112_out, not_113_out, not_114_out);
  and and_19 (and_19_out, not_115_out, not_116_out, F12, OP6, OP5, not_117_out, not_118_out, not_119_out);
  and and_20 (and_20_out, not_120_out, not_121_out, not_122_out, OP6, OP5, not_123_out, not_124_out, OP2);
  and and_21 (and_21_out, not_125_out, not_126_out, F14, not_127_out, F12, not_128_out, OP5, OP4, not_129_out, not_130_out);
  and and_22 (and_22_out, not_131_out, not_132_out, not_133_out, not_134_out, not_135_out, not_136_out, not_137_out, not_138_out);
  and and_23 (and_23_out, F14, F13, not_139_out, OP6, OP5, not_140_out, not_141_out, not_142_out);
  and and_24 (and_24_out, not_143_out, not_144_out, not_145_out, not_146_out, not_147_out, not_148_out, OP5, OP4, not_149_out, not_150_out);
  and and_25 (and_25_out, F30, not_151_out, not_152_out, not_153_out, not_154_out, not_155_out, OP5, OP4, not_156_out, not_157_out);
  and and_26 (and_26_out, not_158_out, not_159_out, F14, F13, F12, not_160_out, OP5, OP4, not_161_out, not_162_out);
  and and_27 (and_27_out, not_163_out, not_164_out, F14, F13, not_165_out, not_166_out, OP5, OP4, not_167_out, not_168_out);
  and and_28 (and_28_out, not_169_out, not_170_out, not_171_out, F13, not_172_out, not_173_out, OP5, OP4, not_174_out, not_175_out);
  and and_29 (and_29_out, not_176_out, not_177_out, not_178_out, F13, F12, not_179_out, OP5, OP4, not_180_out, not_181_out);
  and and_30 (and_30_out, not_182_out, F13, not_183_out, not_184_out, OP5, not_185_out, not_186_out, not_187_out);
  and and_31 (and_31_out, not_188_out, not_189_out, not_190_out, not_191_out, not_192_out, OP6, OP5, OP4, not_193_out, not_194_out);
  and and_32 (and_32_out, not_195_out, not_196_out, not_197_out, OP6, OP5, not_198_out, not_199_out, not_200_out);
  and and_33 (and_33_out, not_201_out, not_202_out, F12, OP6, OP5, not_203_out, not_204_out, not_205_out);
  and and_34 (and_34_out, not_206_out, not_207_out, F14, not_208_out, F12, not_209_out, OP5, OP4, not_210_out, not_211_out);
  and and_35 (and_35_out, F14, F13, not_212_out, OP6, OP5, not_213_out, not_214_out, not_215_out);
  or or_1 (R2Use, and_24_out, and_25_out, and_26_out, and_27_out, and_28_out, and_29_out, and_30_out, and_31_out, and_32_out, and_33_out, and_34_out, and_35_out);
  or or_2 (R1Use, and_1_out, and_2_out, and_3_out, and_4_out, and_5_out, and_6_out, and_7_out, and_8_out, and_9_out, and_10_out, and_11_out, and_12_out, and_13_out, and_14_out, and_15_out, and_16_out, and_17_out, and_18_out, and_19_out, and_20_out, and_21_out, and_22_out, and_23_out);
endmodule

module \寄存器使用情况  (
  input  [4:0] OP,
  input  [4:0] Ex_OPCode,
  input  [4:0] Funct,
  input  [4:0] R1,
  input  [4:0] R2,
  input  ExRegWrite,
  input  [4:0] ExReg_num,
  input  MemRegWrite,
  input  [4:0] MemReg_num,
  output LoadUse,
  output R1ExRelate,
  output R2ExRelate,
  output Hazzard,
  output R1MemRelate,
  output R2MemRelate
);

  wire comparator_1_eq, comparator_2_eq, comparator_3_eq, comparator_4_eq, comparator_5_eq, comparator_6_eq,
       comparator_7_eq, comparator_8_eq, comparator_9_eq, or_1_out, \寄存器使用情况自动生成_1_r1use ,
       \寄存器使用情况自动生成_1_r2use ;

  \寄存器使用情况自动生成  \u_寄存器使用情况自动生成_1  (
    .OP2(OP[0]), .OP3(OP[1]), .OP4(OP[2]), .OP5(OP[3]), .OP6(OP[4]), .F12(Funct[0]), .F13(Funct[1]),
    .F14(Funct[2]), .F25(Funct[3]), .F30(Funct[4]), .R1Use(\寄存器使用情况自动生成_1_r1use ),
    .R2Use(\寄存器使用情况自动生成_1_r2use ));
  Comparator #(.width(5), .mode("twosComplement")) comparator_1 (
    .a(R1), .b({5{1'b0}}), .eq(comparator_1_eq));  // open: gt, lt
  Comparator #(.width(5), .mode("twosComplement")) comparator_2 (
    .a(R1), .b(ExReg_num), .eq(comparator_2_eq));  // open: gt, lt
  Comparator #(.width(5), .mode("twosComplement")) comparator_3 (
    .a(R2), .b({5{1'b0}}), .eq(comparator_3_eq));  // open: gt, lt
  Comparator #(.width(5), .mode("twosComplement")) comparator_4 (
    .a(R2), .b(ExReg_num), .eq(comparator_4_eq));  // open: gt, lt
  Comparator #(.width(5), .mode("twosComplement")) comparator_5 (
    .a(R1), .b({5{1'b0}}), .eq(comparator_5_eq));  // open: gt, lt
  Comparator #(.width(5), .mode("twosComplement")) comparator_6 (
    .a(R1), .b(MemReg_num), .eq(comparator_6_eq));  // open: gt, lt
  Comparator #(.width(5), .mode("twosComplement")) comparator_7 (
    .a(R2), .b({5{1'b0}}), .eq(comparator_7_eq));  // open: gt, lt
  Comparator #(.width(5), .mode("twosComplement")) comparator_8 (
    .a(R2), .b(MemReg_num), .eq(comparator_8_eq));  // open: gt, lt
  and and_1 (R1ExRelate, \寄存器使用情况自动生成_1_r1use , ~comparator_1_eq, ExRegWrite, comparator_2_eq);  // AND_Gate
  and and_2 (R2ExRelate, \寄存器使用情况自动生成_1_r2use , ~comparator_3_eq, ExRegWrite, comparator_4_eq);  // AND_Gate
  and and_3 (R1MemRelate, \寄存器使用情况自动生成_1_r1use , ~comparator_5_eq, MemRegWrite, comparator_6_eq);  // AND_Gate
  and and_4 (R2MemRelate, \寄存器使用情况自动生成_1_r2use , ~comparator_7_eq, MemRegWrite, comparator_8_eq);  // AND_Gate
  Comparator #(.width(5), .mode("twosComplement")) comparator_9 (
    .a({5{1'b0}}), .b(Ex_OPCode), .eq(comparator_9_eq));  // open: gt, lt
  and and_5 (LoadUse, comparator_9_eq, or_1_out);
  or or_1 (or_1_out, R2ExRelate, R1ExRelate);
  or or_2 (Hazzard, R1ExRelate, R2ExRelate, R1MemRelate, R2MemRelate);
endmodule
